// Digital circuit 2bit_mux.dig as structural Verilog
module _2bit_mux (
  input  S,
  input  A,
  input  B,
  output OUT
);

  wire nand_1_out, nand_2_out, nand_3_out;

  nand nand_1 (nand_1_out, S, S);
  nand nand_2 (nand_2_out, A, nand_1_out);
  nand nand_3 (nand_3_out, S, B);
  nand nand_4 (OUT, nand_2_out, nand_3_out);
endmodule
