// Digital circuit 2x16bit_mux.dig as structural Verilog
module _2x16bit_mux (
  input  SEL,
  input  [15:0] A,
  input  [15:0] B,
  output [15:0] OUT
);

  _2x8bit_mux _2x8bit_mux_1 (.SEL(SEL), .B(A[7:0]), .A(B[7:0]), .OUT(OUT[7:0]));
  _2x8bit_mux _2x8bit_mux_2 (.SEL(SEL), .B(A[15:8]), .A(B[15:8]), .OUT(OUT[15:8]));
endmodule
