// Digital circuit 3bit_decode.dig as structural Verilog
module _3bit_decode (
  input  [2:0] IN,
  output [7:0] OUT
);

  wire nand_1_out, nand_2_out, nand_3_out, nand_4_out, nand_5_out, nand_6_out, nand_7_out, nand_8_out,
       nand_9_out, nand_10_out, nand_11_out, nand_12_out, nand_13_out, nand_14_out, nand_15_out, nand_16_out,
       nand_17_out, nand_18_out, nand_19_out, nand_20_out, nand_21_out, nand_22_out, nand_23_out,
       nand_24_out, nand_25_out, nand_26_out, nand_27_out;

  nand nand_1 (nand_1_out, IN[0], IN[0]);
  nand nand_2 (nand_2_out, IN[1], IN[1]);
  nand nand_3 (nand_3_out, IN[2], IN[2]);
  nand nand_4 (nand_4_out, nand_1_out, nand_2_out);
  nand nand_5 (nand_5_out, IN[0], nand_2_out);
  nand nand_6 (nand_6_out, nand_1_out, IN[1]);
  nand nand_7 (nand_7_out, IN[0], IN[1]);
  nand nand_8 (nand_8_out, nand_1_out, nand_2_out);
  nand nand_9 (nand_9_out, IN[0], nand_2_out);
  nand nand_10 (nand_10_out, nand_1_out, IN[1]);
  nand nand_11 (nand_11_out, IN[0], IN[1]);
  nand nand_12 (nand_12_out, nand_4_out, nand_4_out);
  nand nand_13 (nand_13_out, nand_5_out, nand_5_out);
  nand nand_14 (nand_14_out, nand_6_out, nand_6_out);
  nand nand_15 (nand_15_out, nand_7_out, nand_7_out);
  nand nand_16 (nand_16_out, nand_8_out, nand_8_out);
  nand nand_17 (nand_17_out, nand_9_out, nand_9_out);
  nand nand_18 (nand_18_out, nand_10_out, nand_10_out);
  nand nand_19 (nand_19_out, nand_11_out, nand_11_out);
  nand nand_20 (nand_20_out, nand_12_out, nand_3_out);
  nand nand_21 (nand_21_out, nand_13_out, nand_3_out);
  nand nand_22 (nand_22_out, nand_14_out, nand_3_out);
  nand nand_23 (nand_23_out, nand_15_out, nand_3_out);
  nand nand_24 (nand_24_out, nand_16_out, IN[2]);
  nand nand_25 (nand_25_out, nand_17_out, IN[2]);
  nand nand_26 (nand_26_out, nand_18_out, IN[2]);
  nand nand_27 (nand_27_out, nand_19_out, IN[2]);
  nand nand_28 (OUT[0], nand_20_out, nand_20_out);
  nand nand_29 (OUT[1], nand_21_out, nand_21_out);
  nand nand_30 (OUT[2], nand_22_out, nand_22_out);
  nand nand_31 (OUT[3], nand_23_out, nand_23_out);
  nand nand_32 (OUT[4], nand_24_out, nand_24_out);
  nand nand_33 (OUT[5], nand_25_out, nand_25_out);
  nand nand_34 (OUT[6], nand_26_out, nand_26_out);
  nand nand_35 (OUT[7], nand_27_out, nand_27_out);
endmodule
