// Digital circuit 4x8bit_interleave.dig as structural Verilog
module _4x8bit_interleave (
  input  [15:0] WORD0,
  input  [15:0] WORD1,
  input  [15:0] WORD2,
  input  [15:0] WORD3,
  output [3:0] OUT0,
  output [3:0] OUT1,
  output [3:0] OUT2,
  output [3:0] OUT3,
  output [3:0] OUT4,
  output [3:0] OUT5,
  output [3:0] OUT6,
  output [3:0] OUT7
);

  // Pins of 8 and 16 bits meet at WORD0
  // Pins of 8 and 16 bits meet at WORD1
  // Pins of 8 and 16 bits meet at WORD2
  // Pins of 8 and 16 bits meet at WORD3

  assign OUT0 = {WORD3[0], WORD2[0], WORD1[0], WORD0[0]};
  assign OUT1 = {WORD3[1], WORD2[1], WORD1[1], WORD0[1]};
  assign OUT2 = {WORD3[2], WORD2[2], WORD1[2], WORD0[2]};
  assign OUT3 = {WORD3[3], WORD2[3], WORD1[3], WORD0[3]};
  assign OUT4 = {WORD3[4], WORD2[4], WORD1[4], WORD0[4]};
  assign OUT5 = {WORD3[5], WORD2[5], WORD1[5], WORD0[5]};
  assign OUT6 = {WORD3[6], WORD2[6], WORD1[6], WORD0[6]};
  assign OUT7 = {WORD3[7], WORD2[7], WORD1[7], WORD0[7]};
endmodule
