// Digital circuit 4x8bit_mux.dig as structural Verilog
module _4x8bit_mux (
  input  [1:0] SEL,
  input  [7:0] IN0,
  input  [7:0] IN1,
  input  [7:0] IN2,
  input  [7:0] IN3,
  output [15:0] OUT
);

  wire [3:0] _4x8bit_interleave_1_out0, _4x8bit_interleave_1_out1, _4x8bit_interleave_1_out2,
       _4x8bit_interleave_1_out3, _4x8bit_interleave_1_out4, _4x8bit_interleave_1_out5,
       _4x8bit_interleave_1_out6, _4x8bit_interleave_1_out7, select2_1_o3;

  select2 select2_1 (
    .S0(SEL[0]), .S1(SEL[1]), .O0(select2_1_o3[0]), .O1(select2_1_o3[1]), .O2(select2_1_o3[2]),
    .O3(select2_1_o3[3]));
  _4x8bit_interleave _4x8bit_interleave_1 (
    .WORD0(IN0), .WORD1(IN1), .WORD2(IN2), .WORD3(IN3), .OUT0(_4x8bit_interleave_1_out0),
    .OUT1(_4x8bit_interleave_1_out1), .OUT2(_4x8bit_interleave_1_out2), .OUT3(_4x8bit_interleave_1_out3),
    .OUT4(_4x8bit_interleave_1_out4), .OUT5(_4x8bit_interleave_1_out5), .OUT6(_4x8bit_interleave_1_out6),
    .OUT7(_4x8bit_interleave_1_out7));
  deselect2 deselect2_1 (.BI(_4x8bit_interleave_1_out0), .AI(select2_1_o3), .O(OUT[0]));
  deselect2 deselect2_2 (.BI(_4x8bit_interleave_1_out1), .AI(select2_1_o3), .O(OUT[1]));
  deselect2 deselect2_3 (.BI(_4x8bit_interleave_1_out2), .AI(select2_1_o3), .O(OUT[2]));
  deselect2 deselect2_4 (.BI(_4x8bit_interleave_1_out3), .AI(select2_1_o3), .O(OUT[3]));
  deselect2 deselect2_5 (.BI(_4x8bit_interleave_1_out4), .AI(select2_1_o3), .O(OUT[4]));
  deselect2 deselect2_6 (.BI(_4x8bit_interleave_1_out5), .AI(select2_1_o3), .O(OUT[5]));
  deselect2 deselect2_7 (.BI(_4x8bit_interleave_1_out6), .AI(select2_1_o3), .O(OUT[6]));
  deselect2 deselect2_8 (.BI(_4x8bit_interleave_1_out7), .AI(select2_1_o3), .O(OUT[7]));
  // Pins of 8 and 16 bits meet at OUT
endmodule
