// Digital circuit 8bit_alu.dig as structural Verilog
module _8bit_alu (
  input  [3:0] OP,
  input  [7:0] A,
  input  [7:0] B,
  input  CIN,
  output [7:0] RESULT,
  output ZERO,
  output CARRY,
  output OVERFLOW,
  output NEGATIVE
);

  wire _2bit_mux_1_out, _8bit_add_sub_1_cout, _8bit_add_sub_1_overflow, _8bit_shifter_1_out, nand_1_out,
       nand_2_out, nand_3_out, or_1_out;
  wire [7:0] _2x8bit_mux_1_out, _2x8bit_mux_2_out, _8bit_add_sub_1_result, _8bit_or_nor_xor_and_1_result,
       _8bit_shifter_1_result;

  _8bit_add_sub _8bit_add_sub_1 (
    .A(A), .B(B), .ADD_SUB(OP[0]), .CIN(CIN), .RESULT(_8bit_add_sub_1_result), .COUT(_8bit_add_sub_1_cout),
    .OVERFLOW(_8bit_add_sub_1_overflow));
  _8bit_or_nor_xor_and _8bit_or_nor_xor_and_1 (.SEL(OP[1:0]), .A(A), .B(B), .RESULT(_8bit_or_nor_xor_and_1_result));
  _8bit_shifter _8bit_shifter_1 (.A(A), .B(B), .DIR(OP[0]), .RESULT(_8bit_shifter_1_result), .OUT(_8bit_shifter_1_out));
  _2x8bit_mux _2x8bit_mux_1 (
    .SEL(OP[1]), .B(_8bit_shifter_1_result), .A(_8bit_add_sub_1_result), .OUT(_2x8bit_mux_1_out));
  _2x8bit_mux _2x8bit_mux_2 (
    .SEL(OP[2]), .B(_8bit_or_nor_xor_and_1_result), .A(_2x8bit_mux_1_out), .OUT(_2x8bit_mux_2_out));
  nand nand_1 (nand_1_out, OP[2], OP[2]);
  nand nand_2 (nand_2_out, OP[1], OP[1]);
  nand nand_3 (nand_3_out, nand_1_out, nand_2_out);
  _2x8bit_mux _2x8bit_mux_3 (.SEL(OP[3]), .B(B), .A(_2x8bit_mux_2_out), .OUT({NEGATIVE, RESULT[6:0]}));
  _2bit_mux _2bit_mux_1 (.S(OP[1]), .A(_8bit_add_sub_1_cout), .B(_8bit_shifter_1_out), .OUT(_2bit_mux_1_out));
  or or_1 (or_1_out, RESULT[0], RESULT[1], RESULT[2], RESULT[3], RESULT[4], RESULT[5], RESULT[6], NEGATIVE);
  nand nand_4 (ZERO, or_1_out, or_1_out);
  _2bit_mux _2bit_mux_2 (.S(OP[2]), .A(_2bit_mux_1_out), .B(1'b0), .OUT(CARRY));
  _2bit_mux _2bit_mux_3 (.S(nand_3_out), .A(_8bit_add_sub_1_overflow), .B(1'b0), .OUT(OVERFLOW));

  assign RESULT[7] = NEGATIVE;

  // Notes on the sheet:
  //   Schottky Diode OR
endmodule
