// Digital circuit 8bit_half_adder.dig as structural Verilog
module _8bit_half_adder (
  input  [7:0] WORD,
  input  CIN,
  output [7:0] RESULT,
  output COUT
);

  wire half_adder_1_c, half_adder_2_c, half_adder_3_c, half_adder_4_c, half_adder_5_c, half_adder_6_c,
       half_adder_7_c;

  half_adder half_adder_1 (.A(WORD[0]), .B(CIN), .C(half_adder_1_c), .S(RESULT[0]));
  half_adder half_adder_2 (.A(WORD[1]), .B(half_adder_1_c), .C(half_adder_2_c), .S(RESULT[1]));
  half_adder half_adder_3 (.A(WORD[2]), .B(half_adder_2_c), .C(half_adder_3_c), .S(RESULT[2]));
  half_adder half_adder_4 (.A(WORD[3]), .B(half_adder_3_c), .C(half_adder_4_c), .S(RESULT[3]));
  half_adder half_adder_5 (.A(WORD[4]), .B(half_adder_4_c), .C(half_adder_5_c), .S(RESULT[4]));
  half_adder half_adder_6 (.A(WORD[5]), .B(half_adder_5_c), .C(half_adder_6_c), .S(RESULT[5]));
  half_adder half_adder_7 (.A(WORD[6]), .B(half_adder_6_c), .C(half_adder_7_c), .S(RESULT[6]));
  half_adder half_adder_8 (.A(WORD[7]), .B(half_adder_7_c), .C(COUT), .S(RESULT[7]));
  // Pins of 1 and 8 bits meet at WORD
  // Pins of 1 and 8 bits meet at RESULT
endmodule
