// Digital circuit 8bit_masked_or.dig as structural Verilog
module _8bit_masked_or (
  input  [7:0] DATA,
  input  [7:0] MASK,
  output OUT
);

  wire nand_1_out, nand_2_out, nand_3_out, nand_4_out, nand_5_out, nand_6_out, nand_7_out, nand_8_out,
       nand_9_out, nand_10_out, nand_11_out, nand_12_out, nand_13_out, nand_14_out, nand_15_out, nand_16_out;

  nand nand_1 (nand_1_out, DATA[0], MASK[0]);
  nand nand_2 (nand_2_out, DATA[1], MASK[1]);
  nand nand_3 (nand_3_out, DATA[2], MASK[2]);
  nand nand_4 (nand_4_out, DATA[3], MASK[3]);
  nand nand_5 (nand_5_out, DATA[4], MASK[4]);
  nand nand_6 (nand_6_out, DATA[5], MASK[5]);
  nand nand_7 (nand_7_out, DATA[6], MASK[6]);
  nand nand_8 (nand_8_out, DATA[7], MASK[7]);
  nand nand_9 (nand_9_out, nand_1_out, nand_1_out);
  nand nand_10 (nand_10_out, nand_2_out, nand_2_out);
  nand nand_11 (nand_11_out, nand_3_out, nand_3_out);
  nand nand_12 (nand_12_out, nand_4_out, nand_4_out);
  nand nand_13 (nand_13_out, nand_5_out, nand_5_out);
  nand nand_14 (nand_14_out, nand_6_out, nand_6_out);
  nand nand_15 (nand_15_out, nand_7_out, nand_7_out);
  nand nand_16 (nand_16_out, nand_8_out, nand_8_out);
  or or_1 (OUT, nand_9_out, nand_10_out, nand_11_out, nand_12_out, nand_13_out, nand_14_out, nand_15_out, nand_16_out);

  // Notes on the sheet:
  //   Schottky OR
endmodule
