// Digital circuit 8x8bit_masked_or.dig as structural Verilog
module _8x8bit_masked_or (
  input  [2:0] SELECT,
  input  [7:0] DATA0,
  input  [7:0] DATA1,
  input  [7:0] DATA2,
  input  [7:0] DATA3,
  input  [7:0] DATA4,
  input  [7:0] DATA5,
  input  [7:0] DATA6,
  input  [7:0] DATA7,
  output OUT0,
  output OUT1,
  output OUT2,
  output OUT3,
  output OUT4,
  output OUT5,
  output OUT6,
  output OUT7
);

  wire [7:0] _3bit_decode_1_out;

  _3bit_decode _3bit_decode_1 (.IN(SELECT), .OUT(_3bit_decode_1_out));
  _8bit_masked_or _8bit_masked_or_1 (.DATA(DATA0), .MASK(_3bit_decode_1_out), .OUT(OUT0));
  _8bit_masked_or _8bit_masked_or_2 (.DATA(DATA1), .MASK(_3bit_decode_1_out), .OUT(OUT1));
  _8bit_masked_or _8bit_masked_or_3 (.DATA(DATA2), .MASK(_3bit_decode_1_out), .OUT(OUT2));
  _8bit_masked_or _8bit_masked_or_4 (.DATA(DATA3), .MASK(_3bit_decode_1_out), .OUT(OUT3));
  _8bit_masked_or _8bit_masked_or_5 (.DATA(DATA4), .MASK(_3bit_decode_1_out), .OUT(OUT4));
  _8bit_masked_or _8bit_masked_or_6 (.DATA(DATA5), .MASK(_3bit_decode_1_out), .OUT(OUT5));
  _8bit_masked_or _8bit_masked_or_7 (.DATA(DATA6), .MASK(_3bit_decode_1_out), .OUT(OUT6));
  _8bit_masked_or _8bit_masked_or_8 (.DATA(DATA7), .MASK(_3bit_decode_1_out), .OUT(OUT7));
endmodule
