// Digital circuit clock.dig as structural Verilog
module clock (
  input  RESET,
  input  HALT,
  input  CONTINUE,
  input  CLKHALT,
  input  CLKIN,
  output ISHALTED,
  output RESET_2,
  output CLKOUT
);

  wire nand_1_out, nand_2_out, nand_3_out, nand_4_out, nand_5_out, nand_6_out, nand_9_out, nand_10_out,
       nand_11_out, nand_12_out, nand_13_out;

  nand nand_1 (nand_1_out, HALT, HALT);
  nand nand_2 (nand_2_out, RESET, RESET);
  nand nand_3 (nand_3_out, nand_12_out, nand_12_out);
  nand nand_4 (nand_4_out, CLKIN, CLKIN);
  nand nand_5 (nand_5_out, nand_1_out, nand_2_out);
  nand nand_6 (nand_6_out, nand_3_out, CONTINUE);
  nand nand_7 (RESET_2, RESET, RESET);
  nand nand_8 (ISHALTED, nand_3_out, nand_9_out);
  nand nand_9 (nand_9_out, ISHALTED, nand_6_out);
  nand nand_10 (nand_10_out, nand_5_out, nand_5_out);
  nand nand_11 (nand_11_out, nand_4_out, CLKHALT);
  nand nand_12 (nand_12_out, nand_10_out, nand_11_out);
  nand nand_13 (nand_13_out, CLKIN, nand_9_out);
  nand nand_14 (CLKOUT, nand_13_out, nand_13_out);
endmodule
