// Digital circuit condition_checker.dig as structural Verilog
module condition_checker (
  input  [4:0] FLAGS,
  input  [2:0] COND,
  output SKIP
);

  wire nand_1_out, nand_2_out, nand_3_out, nand_4_out, nand_5_out, nand_6_out, nand_7_out, nand_8_out,
       nand_9_out, nand_10_out, nand_11_out, nand_12_out, nand_13_out, nand_14_out, nand_15_out, nand_16_out,
       nand_17_out, nand_18_out, nand_19_out, or_1_out, select3_1_o0, select3_1_o1, select3_1_o2,
       select3_1_o3, select3_1_o4, select3_1_o5, select3_1_o6, select3_1_o7;

  select3 select3_1 (
    .S2(COND[2]), .S1(COND[1]), .S0(COND[0]), .O0(select3_1_o0), .O1(select3_1_o1), .O2(select3_1_o2),
    .O3(select3_1_o3), .O4(select3_1_o4), .O5(select3_1_o5), .O6(select3_1_o6), .O7(select3_1_o7));
  nand nand_1 (nand_1_out, FLAGS[2], FLAGS[2]);
  nand nand_2 (nand_2_out, FLAGS[4], FLAGS[4]);
  nand nand_3 (nand_3_out, FLAGS[0], select3_1_o1);
  nand nand_4 (nand_4_out, FLAGS[1], select3_1_o2);
  nand nand_5 (nand_5_out, FLAGS[2], select3_1_o3);
  nand nand_6 (nand_6_out, FLAGS[3], select3_1_o4);
  nand nand_7 (nand_7_out, FLAGS[4], select3_1_o5);
  nand nand_8 (nand_8_out, nand_1_out, select3_1_o6);
  nand nand_9 (nand_9_out, nand_2_out, select3_1_o7);
  nand nand_10 (nand_10_out, nand_3_out, nand_3_out);
  nand nand_11 (nand_11_out, nand_4_out, nand_4_out);
  nand nand_12 (nand_12_out, nand_5_out, nand_5_out);
  nand nand_13 (nand_13_out, nand_6_out, nand_6_out);
  nand nand_14 (nand_14_out, nand_7_out, nand_7_out);
  nand nand_15 (nand_15_out, nand_8_out, nand_8_out);
  nand nand_16 (nand_16_out, nand_9_out, nand_9_out);
  or or_1 (or_1_out, nand_10_out, nand_11_out, nand_12_out, nand_13_out, nand_14_out, nand_15_out, nand_16_out);
  nand nand_17 (nand_17_out, select3_1_o0, select3_1_o0);
  nand nand_18 (nand_18_out, or_1_out, or_1_out);
  nand nand_19 (nand_19_out, nand_17_out, nand_18_out);
  nand nand_20 (SKIP, nand_19_out, nand_19_out);
endmodule
