// Digital circuit deselect2.dig as structural Verilog
module deselect2 (
  input  [3:0] BI,
  input  [3:0] AI,
  output O
);

  wire nand_1_out, nand_2_out, nand_3_out, nand_4_out, nand_5_out, nand_6_out, nand_7_out, nand_8_out;

  nand nand_1 (nand_1_out, AI[0], BI[0]);
  nand nand_2 (nand_2_out, AI[1], BI[1]);
  nand nand_3 (nand_3_out, AI[2], BI[2]);
  nand nand_4 (nand_4_out, AI[3], BI[3]);
  nand nand_5 (nand_5_out, nand_1_out, nand_2_out);
  nand nand_6 (nand_6_out, nand_3_out, nand_4_out);
  nand nand_7 (nand_7_out, nand_5_out, nand_5_out);
  nand nand_8 (nand_8_out, nand_6_out, nand_6_out);
  nand nand_9 (O, nand_7_out, nand_8_out);
endmodule
