// Digital circuit half_adder.dig as structural Verilog
module half_adder (
  input  A,
  input  B,
  output C,
  output S
);

  wire nand_1_out, nand_2_out, nand_3_out;

  nand nand_1 (nand_1_out, A, B);
  nand nand_2 (nand_2_out, A, nand_1_out);
  nand nand_3 (nand_3_out, nand_1_out, B);
  nand nand_4 (S, nand_2_out, nand_3_out);
  nand nand_5 (C, nand_1_out, nand_1_out);
endmodule
