// Digital circuit out_register.dig as structural Verilog
module out_register (
  input  [7:0] DATA,
  input  WEN,
  output [7:0] OUT
);

  wire nand_1_out, nand_2_out, nand_3_out, nand_4_out, nand_5_out, nand_6_out, nand_7_out, nand_8_out,
       nand_9_out, nand_10_out, nand_11_out, nand_12_out, nand_13_out, nand_14_out, nand_15_out, nand_16_out,
       nand_18_out, nand_20_out, nand_22_out, nand_24_out, nand_26_out, nand_28_out, nand_30_out, nand_32_out;

  nand nand_1 (nand_1_out, DATA[0], WEN);
  nand nand_2 (nand_2_out, nand_1_out, WEN);
  nand nand_3 (nand_3_out, DATA[1], WEN);
  nand nand_4 (nand_4_out, nand_3_out, WEN);
  nand nand_5 (nand_5_out, DATA[2], WEN);
  nand nand_6 (nand_6_out, nand_5_out, WEN);
  nand nand_7 (nand_7_out, DATA[3], WEN);
  nand nand_8 (nand_8_out, nand_7_out, WEN);
  nand nand_9 (nand_9_out, DATA[4], WEN);
  nand nand_10 (nand_10_out, nand_9_out, WEN);
  nand nand_11 (nand_11_out, DATA[5], WEN);
  nand nand_12 (nand_12_out, nand_11_out, WEN);
  nand nand_13 (nand_13_out, DATA[6], WEN);
  nand nand_14 (nand_14_out, nand_13_out, WEN);
  nand nand_15 (nand_15_out, DATA[7], WEN);
  nand nand_16 (nand_16_out, nand_15_out, WEN);
  nand nand_17 (OUT[0], nand_1_out, nand_18_out);
  nand nand_18 (nand_18_out, OUT[0], nand_2_out);
  nand nand_19 (OUT[1], nand_3_out, nand_20_out);
  nand nand_20 (nand_20_out, OUT[1], nand_4_out);
  nand nand_21 (OUT[2], nand_5_out, nand_22_out);
  nand nand_22 (nand_22_out, OUT[2], nand_6_out);
  nand nand_23 (OUT[3], nand_7_out, nand_24_out);
  nand nand_24 (nand_24_out, OUT[3], nand_8_out);
  nand nand_25 (OUT[4], nand_9_out, nand_26_out);
  nand nand_26 (nand_26_out, OUT[4], nand_10_out);
  nand nand_27 (OUT[5], nand_11_out, nand_28_out);
  nand nand_28 (nand_28_out, OUT[5], nand_12_out);
  nand nand_29 (OUT[6], nand_13_out, nand_30_out);
  nand nand_30 (nand_30_out, OUT[6], nand_14_out);
  nand nand_31 (OUT[7], nand_15_out, nand_32_out);
  nand nand_32 (nand_32_out, OUT[7], nand_16_out);
endmodule
