// Digital circuit program_counter.dig as structural Verilog
module program_counter (
  input  CLK,
  input  [15:0] W,
  output [15:0] R
);

  register register_1 (.CLK(CLK), .WEN(1'b1), .WRITE(W[7:0]), .READ(R[7:0]));
  register register_2 (.CLK(CLK), .WEN(1'b1), .WRITE(W[15:8]), .READ(R[15:8]));
endmodule
