// Digital circuit register_file.dig as structural Verilog
module register_file (
  input  CLK,
  input  WEN,
  input  [7:0] WRITE,
  input  [2:0] R2SEL,
  input  [2:0] R1SEL,
  input  [2:0] WSEL,
  output [7:0] READ1,
  output [7:0] READ2,
  output [7:0] READP
);

  wire nand_1_out, nand_2_out, nand_3_out, nand_4_out, nand_5_out, nand_6_out, nand_7_out, nand_8_out,
       nand_9_out, nand_10_out, nand_11_out, nand_12_out, nand_13_out, nand_14_out, nand_15_out, nand_16_out,
       select3_1_o0, select3_1_o1, select3_1_o2, select3_1_o3, select3_1_o4, select3_1_o5, select3_1_o6,
       select3_1_o7;
  wire [7:0] _8x8bit_interleave_1_out0, _8x8bit_interleave_1_out1, _8x8bit_interleave_1_out2,
       _8x8bit_interleave_1_out3, _8x8bit_interleave_1_out4, _8x8bit_interleave_1_out5,
       _8x8bit_interleave_1_out6, _8x8bit_interleave_1_out7, register_1_read, register_2_read,
       register_3_read, register_4_read, register_5_read, register_6_read, register_7_read, select3_2_o7,
       select3_3_o7;

  select3 select3_1 (
    .S2(WSEL[2]), .S1(WSEL[1]), .S0(WSEL[0]), .O0(select3_1_o0), .O1(select3_1_o1), .O2(select3_1_o2),
    .O3(select3_1_o3), .O4(select3_1_o4), .O5(select3_1_o5), .O6(select3_1_o6), .O7(select3_1_o7));
  select3 select3_2 (
    .S2(R1SEL[2]), .S1(R1SEL[1]), .S0(R1SEL[0]), .O0(select3_2_o7[0]), .O1(select3_2_o7[1]),
    .O2(select3_2_o7[2]), .O3(select3_2_o7[3]), .O4(select3_2_o7[4]), .O5(select3_2_o7[5]),
    .O6(select3_2_o7[6]), .O7(select3_2_o7[7]));
  select3 select3_3 (
    .S2(R2SEL[2]), .S1(R2SEL[1]), .S0(R2SEL[0]), .O0(select3_3_o7[0]), .O1(select3_3_o7[1]),
    .O2(select3_3_o7[2]), .O3(select3_3_o7[3]), .O4(select3_3_o7[4]), .O5(select3_3_o7[5]),
    .O6(select3_3_o7[6]), .O7(select3_3_o7[7]));
  nand nand_1 (nand_1_out, WEN, select3_1_o0);
  nand nand_2 (nand_2_out, WEN, select3_1_o1);
  nand nand_3 (nand_3_out, WEN, select3_1_o2);
  nand nand_4 (nand_4_out, WEN, select3_1_o3);
  nand nand_5 (nand_5_out, WEN, select3_1_o4);
  nand nand_6 (nand_6_out, WEN, select3_1_o5);
  nand nand_7 (nand_7_out, WEN, select3_1_o6);
  nand nand_8 (nand_8_out, WEN, select3_1_o7);
  nand nand_9 (nand_9_out, nand_1_out, nand_1_out);
  nand nand_10 (nand_10_out, nand_2_out, nand_2_out);
  nand nand_11 (nand_11_out, nand_3_out, nand_3_out);
  nand nand_12 (nand_12_out, nand_4_out, nand_4_out);
  nand nand_13 (nand_13_out, nand_5_out, nand_5_out);
  nand nand_14 (nand_14_out, nand_6_out, nand_6_out);
  nand nand_15 (nand_15_out, nand_7_out, nand_7_out);
  nand nand_16 (nand_16_out, nand_8_out, nand_8_out);
  register register_1 (.CLK(CLK), .WEN(nand_9_out), .WRITE(WRITE), .READ(register_1_read));
  register register_2 (.CLK(CLK), .WEN(nand_10_out), .WRITE(WRITE), .READ(register_2_read));
  register register_3 (.CLK(CLK), .WEN(nand_11_out), .WRITE(WRITE), .READ(register_3_read));
  register register_4 (.CLK(CLK), .WEN(nand_12_out), .WRITE(WRITE), .READ(register_4_read));
  register register_5 (.CLK(CLK), .WEN(nand_13_out), .WRITE(WRITE), .READ(register_5_read));
  register register_6 (.CLK(CLK), .WEN(nand_14_out), .WRITE(WRITE), .READ(register_6_read));
  register register_7 (.CLK(CLK), .WEN(nand_15_out), .WRITE(WRITE), .READ(register_7_read));
  register register_8 (.CLK(CLK), .WEN(nand_16_out), .WRITE(WRITE), .READ(READP));
  deselect3 deselect3_1 (.BI(_8x8bit_interleave_1_out0), .AI(select3_2_o7), .O(READ1[0]));
  deselect3 deselect3_2 (.BI(_8x8bit_interleave_1_out0), .AI(select3_3_o7), .O(READ2[0]));
  deselect3 deselect3_3 (.BI(_8x8bit_interleave_1_out1), .AI(select3_2_o7), .O(READ1[1]));
  deselect3 deselect3_4 (.BI(_8x8bit_interleave_1_out1), .AI(select3_3_o7), .O(READ2[1]));
  deselect3 deselect3_5 (.BI(_8x8bit_interleave_1_out2), .AI(select3_2_o7), .O(READ1[2]));
  deselect3 deselect3_6 (.BI(_8x8bit_interleave_1_out2), .AI(select3_3_o7), .O(READ2[2]));
  deselect3 deselect3_7 (.BI(_8x8bit_interleave_1_out3), .AI(select3_2_o7), .O(READ1[3]));
  deselect3 deselect3_8 (.BI(_8x8bit_interleave_1_out3), .AI(select3_3_o7), .O(READ2[3]));
  _8x8bit_interleave _8x8bit_interleave_1 (
    .WORD0(register_1_read), .WORD1(register_2_read), .WORD2(register_3_read), .WORD3(register_4_read),
    .WORD4(register_5_read), .WORD5(register_6_read), .WORD6(register_7_read), .WORD7(READP),
    .OUT0(_8x8bit_interleave_1_out0), .OUT1(_8x8bit_interleave_1_out1), .OUT2(_8x8bit_interleave_1_out2),
    .OUT3(_8x8bit_interleave_1_out3), .OUT4(_8x8bit_interleave_1_out4), .OUT5(_8x8bit_interleave_1_out5),
    .OUT6(_8x8bit_interleave_1_out6), .OUT7(_8x8bit_interleave_1_out7));
  deselect3 deselect3_9 (.BI(_8x8bit_interleave_1_out4), .AI(select3_2_o7), .O(READ1[4]));
  deselect3 deselect3_10 (.BI(_8x8bit_interleave_1_out4), .AI(select3_3_o7), .O(READ2[4]));
  deselect3 deselect3_11 (.BI(_8x8bit_interleave_1_out5), .AI(select3_2_o7), .O(READ1[5]));
  deselect3 deselect3_12 (.BI(_8x8bit_interleave_1_out5), .AI(select3_3_o7), .O(READ2[5]));
  deselect3 deselect3_13 (.BI(_8x8bit_interleave_1_out6), .AI(select3_2_o7), .O(READ1[6]));
  deselect3 deselect3_14 (.BI(_8x8bit_interleave_1_out6), .AI(select3_3_o7), .O(READ2[6]));
  deselect3 deselect3_15 (.BI(_8x8bit_interleave_1_out7), .AI(select3_2_o7), .O(READ1[7]));
  deselect3 deselect3_16 (.BI(_8x8bit_interleave_1_out7), .AI(select3_3_o7), .O(READ2[7]));
endmodule
