// Digital circuit select3.dig as structural Verilog
module select3 (
  input  S2,
  input  S1,
  input  S0,
  output O0,
  output O1,
  output O2,
  output O3,
  output O4,
  output O5,
  output O6,
  output O7
);

  wire nand_1_out, nand_2_out, nand_3_out, nand_4_out, nand_5_out, nand_6_out, nand_7_out, nand_8_out,
       nand_9_out, nand_10_out, nand_11_out, nand_12_out, nand_13_out, nand_14_out, nand_15_out, nand_16_out,
       nand_17_out, nand_18_out, nand_19_out;

  nand nand_1 (nand_1_out, S2, S2);
  nand nand_2 (nand_2_out, S1, S1);
  nand nand_3 (nand_3_out, S0, S0);
  nand nand_4 (nand_4_out, nand_1_out, nand_2_out);
  nand nand_5 (nand_5_out, nand_1_out, S1);
  nand nand_6 (nand_6_out, S2, nand_2_out);
  nand nand_7 (nand_7_out, S2, S1);
  nand nand_8 (nand_8_out, nand_4_out, nand_4_out);
  nand nand_9 (nand_9_out, nand_5_out, nand_5_out);
  nand nand_10 (nand_10_out, nand_6_out, nand_6_out);
  nand nand_11 (nand_11_out, nand_7_out, nand_7_out);
  nand nand_12 (nand_12_out, nand_8_out, nand_3_out);
  nand nand_13 (nand_13_out, nand_8_out, S0);
  nand nand_14 (nand_14_out, nand_9_out, nand_3_out);
  nand nand_15 (nand_15_out, nand_9_out, S0);
  nand nand_16 (nand_16_out, nand_10_out, nand_3_out);
  nand nand_17 (nand_17_out, nand_10_out, S0);
  nand nand_18 (nand_18_out, nand_11_out, nand_3_out);
  nand nand_19 (nand_19_out, nand_11_out, S0);
  nand nand_20 (O0, nand_12_out, nand_12_out);
  nand nand_21 (O1, nand_13_out, nand_13_out);
  nand nand_22 (O2, nand_14_out, nand_14_out);
  nand nand_23 (O3, nand_15_out, nand_15_out);
  nand nand_24 (O4, nand_16_out, nand_16_out);
  nand nand_25 (O5, nand_17_out, nand_17_out);
  nand nand_26 (O6, nand_18_out, nand_18_out);
  nand nand_27 (O7, nand_19_out, nand_19_out);
endmodule
