// Digital circuit select4.dig as structural Verilog
module select4 (
  input  [3:0] SELECT,
  output [15:0] OUT
);

  wire nand_1_out, nand_2_out, nand_3_out, nand_4_out, nand_5_out, nand_6_out, nand_7_out, nand_8_out,
       nand_9_out, nand_10_out, nand_11_out, nand_12_out, nand_13_out, nand_14_out, nand_15_out, nand_16_out,
       nand_17_out, nand_18_out, nand_19_out, nand_20_out, nand_21_out, nand_22_out, nand_23_out,
       nand_24_out, nand_25_out, nand_26_out, nand_27_out, nand_28_out, nand_29_out, nand_30_out,
       nand_31_out, nand_32_out, nand_33_out, nand_34_out, nand_35_out, nand_36_out;

  nand nand_1 (nand_1_out, SELECT[3], SELECT[3]);
  nand nand_2 (nand_2_out, SELECT[2], SELECT[2]);
  nand nand_3 (nand_3_out, SELECT[1], SELECT[1]);
  nand nand_4 (nand_4_out, SELECT[0], SELECT[0]);
  nand nand_5 (nand_5_out, nand_3_out, nand_4_out);
  nand nand_6 (nand_6_out, nand_3_out, SELECT[0]);
  nand nand_7 (nand_7_out, SELECT[1], nand_4_out);
  nand nand_8 (nand_8_out, SELECT[1], SELECT[0]);
  nand nand_9 (nand_9_out, nand_1_out, nand_2_out);
  nand nand_10 (nand_10_out, nand_1_out, SELECT[2]);
  nand nand_11 (nand_11_out, SELECT[3], nand_2_out);
  nand nand_12 (nand_12_out, SELECT[3], SELECT[2]);
  nand nand_13 (nand_13_out, nand_5_out, nand_5_out);
  nand nand_14 (nand_14_out, nand_6_out, nand_6_out);
  nand nand_15 (nand_15_out, nand_7_out, nand_7_out);
  nand nand_16 (nand_16_out, nand_8_out, nand_8_out);
  nand nand_17 (nand_17_out, nand_9_out, nand_9_out);
  nand nand_18 (nand_18_out, nand_10_out, nand_10_out);
  nand nand_19 (nand_19_out, nand_11_out, nand_11_out);
  nand nand_20 (nand_20_out, nand_12_out, nand_12_out);
  nand nand_21 (nand_21_out, nand_17_out, nand_13_out);
  nand nand_22 (nand_22_out, nand_17_out, nand_14_out);
  nand nand_23 (nand_23_out, nand_17_out, nand_15_out);
  nand nand_24 (nand_24_out, nand_17_out, nand_16_out);
  nand nand_25 (nand_25_out, nand_18_out, nand_13_out);
  nand nand_26 (nand_26_out, nand_18_out, nand_14_out);
  nand nand_27 (nand_27_out, nand_18_out, nand_15_out);
  nand nand_28 (nand_28_out, nand_18_out, nand_16_out);
  nand nand_29 (nand_29_out, nand_19_out, nand_13_out);
  nand nand_30 (nand_30_out, nand_19_out, nand_14_out);
  nand nand_31 (nand_31_out, nand_19_out, nand_15_out);
  nand nand_32 (nand_32_out, nand_19_out, nand_16_out);
  nand nand_33 (nand_33_out, nand_20_out, nand_13_out);
  nand nand_34 (nand_34_out, nand_20_out, nand_14_out);
  nand nand_35 (nand_35_out, nand_20_out, nand_15_out);
  nand nand_36 (nand_36_out, nand_20_out, nand_16_out);
  nand nand_37 (OUT[0], nand_21_out, nand_21_out);
  nand nand_38 (OUT[1], nand_22_out, nand_22_out);
  nand nand_39 (OUT[2], nand_23_out, nand_23_out);
  nand nand_40 (OUT[3], nand_24_out, nand_24_out);
  nand nand_41 (OUT[4], nand_25_out, nand_25_out);
  nand nand_42 (OUT[5], nand_26_out, nand_26_out);
  nand nand_43 (OUT[6], nand_27_out, nand_27_out);
  nand nand_44 (OUT[7], nand_28_out, nand_28_out);
  nand nand_45 (OUT[8], nand_29_out, nand_29_out);
  nand nand_46 (OUT[9], nand_30_out, nand_30_out);
  nand nand_47 (OUT[10], nand_31_out, nand_31_out);
  nand nand_48 (OUT[11], nand_32_out, nand_32_out);
  nand nand_49 (OUT[12], nand_33_out, nand_33_out);
  nand nand_50 (OUT[13], nand_34_out, nand_34_out);
  nand nand_51 (OUT[14], nand_35_out, nand_35_out);
  nand nand_52 (OUT[15], nand_36_out, nand_36_out);
endmodule
