// Digital circuit 16bit_incrementer.dig as structural Verilog
module _16bit_incrementer (
  input  [15:0] IN,
  output [15:0] OUT
);

  wire _8bit_half_adder_1_cout;

  _8bit_half_adder _8bit_half_adder_1 (.WORD(IN[7:0]), .CIN(1'b1), .RESULT(OUT[7:0]), .COUT(_8bit_half_adder_1_cout));
  _8bit_half_adder _8bit_half_adder_2 (
    .WORD(IN[15:8]), .CIN(_8bit_half_adder_1_cout), .RESULT(OUT[15:8]));  // open: COUT
endmodule
