// Digital circuit 16x9bit_mux.dig as structural Verilog
module _16x9bit_mux (
  input  [3:0] SEL,
  input  [9:0] IN0,
  input  [9:0] IN1,
  input  [9:0] IN2,
  input  [9:0] IN3,
  input  [9:0] IN4,
  input  [9:0] IN5,
  input  [9:0] IN6,
  input  [9:0] IN7,
  input  [9:0] IN8,
  input  [9:0] IN9,
  input  [9:0] IN10,
  input  [9:0] IN11,
  input  [9:0] IN12,
  input  [9:0] IN13,
  input  [9:0] IN14,
  input  [9:0] IN15,
  output [9:0] OUT
);

  wire select4_1_p2;

  // select4 select4_1: pin names not known; wires that end beside it: SEL, select4_1_p2
  // deselect4 deselect4_1: pin names not known; wires that end beside it: {IN15[0], IN14[0], IN13[0], IN12[0], IN11[0], IN10[0], IN9[0], IN8[0], IN7[0], IN6[0], IN5[0], IN4[0], IN3[0], IN2[0], IN1[0], IN0[0]}, OUT[0], select4_1_p2
  // deselect4 deselect4_2: pin names not known; wires that end beside it: {IN15[1], IN14[1], IN13[1], IN12[1], IN11[1], IN10[1], IN9[1], IN8[1], IN7[1], IN6[1], IN5[1], IN4[1], IN3[1], IN2[1], IN1[1], IN0[1]}, OUT[1], select4_1_p2
  // deselect4 deselect4_3: pin names not known; wires that end beside it: {IN15[2], IN14[2], IN13[2], IN12[2], IN11[2], IN10[2], IN9[2], IN8[2], IN7[2], IN6[2], IN5[2], IN4[2], IN3[2], IN2[2], IN1[2], IN0[2]}, OUT[2], select4_1_p2
  // deselect4 deselect4_4: pin names not known; wires that end beside it: {IN15[3], IN14[3], IN13[3], IN12[3], IN11[3], IN10[3], IN9[3], IN8[3], IN7[3], IN6[3], IN5[3], IN4[3], IN3[3], IN2[3], IN1[3], IN0[3]}, OUT[3], select4_1_p2
  // deselect4 deselect4_5: pin names not known; wires that end beside it: {IN15[4], IN14[4], IN13[4], IN12[4], IN11[4], IN10[4], IN9[4], IN8[4], IN7[4], IN6[4], IN5[4], IN4[4], IN3[4], IN2[4], IN1[4], IN0[4]}, OUT[4], select4_1_p2
  // deselect4 deselect4_6: pin names not known; wires that end beside it: {IN15[5], IN14[5], IN13[5], IN12[5], IN11[5], IN10[5], IN9[5], IN8[5], IN7[5], IN6[5], IN5[5], IN4[5], IN3[5], IN2[5], IN1[5], IN0[5]}, OUT[5], select4_1_p2
  // deselect4 deselect4_7: pin names not known; wires that end beside it: {IN15[6], IN14[6], IN13[6], IN12[6], IN11[6], IN10[6], IN9[6], IN8[6], IN7[6], IN6[6], IN5[6], IN4[6], IN3[6], IN2[6], IN1[6], IN0[6]}, OUT[6], select4_1_p2
  // deselect4 deselect4_8: pin names not known; wires that end beside it: {IN15[7], IN14[7], IN13[7], IN12[7], IN11[7], IN10[7], IN9[7], IN8[7], IN7[7], IN6[7], IN5[7], IN4[7], IN3[7], IN2[7], IN1[7], IN0[7]}, OUT[7], select4_1_p2
  // deselect4 deselect4_9: pin names not known; wires that end beside it: {IN15[8], IN14[8], IN13[8], IN12[8], IN11[8], IN10[8], IN9[8], IN8[8], IN7[8], IN6[8], IN5[8], IN4[8], IN3[8], IN2[8], IN1[8], IN0[8]}, OUT[8], select4_1_p2
  // deselect4 deselect4_10: pin names not known; wires that end beside it: {IN15[9], IN14[9], IN13[9], IN12[9], IN11[9], IN10[9], IN9[9], IN8[9], IN7[9], IN6[9], IN5[9], IN4[9], IN3[9], IN2[9], IN1[9], IN0[9]}, OUT[9], select4_1_p2
endmodule
