// Digital circuit 1bit_or_and_xor_nand.dig as structural Verilog
module _1bit_or_and_xor_nand (
  input  A,
  input  B,
  output [3:0] RESULT
);

  wire nand_1_out, nand_2_out, nand_5_out, nand_6_out;

  nand nand_1 (nand_1_out, A, A);
  nand nand_2 (nand_2_out, B, B);
  nand nand_3 (RESULT[3], A, B);
  nand nand_4 (RESULT[0], nand_1_out, nand_2_out);
  nand nand_5 (nand_5_out, A, RESULT[3]);
  nand nand_6 (nand_6_out, RESULT[3], B);
  nand nand_7 (RESULT[1], RESULT[3], RESULT[3]);
  nand nand_8 (RESULT[2], nand_5_out, nand_6_out);
endmodule
