// Digital circuit 1bit_or_nor_xor_and.dig as structural Verilog
module _1bit_or_nor_xor_and (
  input  A,
  input  B,
  output [3:0] RESULT
);

  wire nand_1_out, nand_2_out, nand_3_out, nand_5_out, nand_6_out;

  nand nand_1 (nand_1_out, A, A);
  nand nand_2 (nand_2_out, B, B);
  nand nand_3 (nand_3_out, A, B);
  nand nand_4 (RESULT[0], nand_1_out, nand_2_out);
  nand nand_5 (nand_5_out, A, nand_3_out);
  nand nand_6 (nand_6_out, nand_3_out, B);
  nand nand_7 (RESULT[1], RESULT[0], RESULT[0]);
  nand nand_8 (RESULT[2], nand_5_out, nand_6_out);
  nand nand_9 (RESULT[3], nand_3_out, nand_3_out);
endmodule
