// Digital circuit 2bit_decode.dig as structural Verilog
module _2bit_decode (
  input  [1:0] IN,
  output [3:0] OUT
);

  wire nand_1_out, nand_2_out, nand_3_out, nand_4_out, nand_5_out, nand_6_out;

  nand nand_1 (nand_1_out, IN[0], IN[0]);
  nand nand_2 (nand_2_out, IN[1], IN[1]);
  nand nand_3 (nand_3_out, nand_1_out, nand_2_out);
  nand nand_4 (nand_4_out, IN[0], nand_2_out);
  nand nand_5 (nand_5_out, nand_1_out, IN[1]);
  nand nand_6 (nand_6_out, IN[0], IN[1]);
  nand nand_7 (OUT[0], nand_3_out, nand_3_out);
  nand nand_8 (OUT[1], nand_4_out, nand_4_out);
  nand nand_9 (OUT[2], nand_5_out, nand_5_out);
  nand nand_10 (OUT[3], nand_6_out, nand_6_out);
endmodule
