// Digital circuit 2x8bit_mux.dig as structural Verilog
module _2x8bit_mux (
  input  SEL,
  input  [7:0] B,
  input  [7:0] A,
  output [7:0] OUT
);

  wire nand_1_out, nand_2_out, nand_3_out, nand_4_out, nand_5_out, nand_6_out, nand_7_out, nand_8_out,
       nand_9_out, nand_10_out, nand_11_out, nand_12_out, nand_13_out, nand_14_out, nand_15_out, nand_16_out,
       nand_17_out;

  nand nand_1 (nand_1_out, SEL, SEL);
  nand nand_2 (nand_2_out, B[0], SEL);
  nand nand_3 (nand_3_out, A[0], nand_1_out);
  nand nand_4 (nand_4_out, B[1], SEL);
  nand nand_5 (nand_5_out, A[1], nand_1_out);
  nand nand_6 (nand_6_out, B[2], SEL);
  nand nand_7 (nand_7_out, A[2], nand_1_out);
  nand nand_8 (nand_8_out, B[3], SEL);
  nand nand_9 (nand_9_out, A[3], nand_1_out);
  nand nand_10 (nand_10_out, B[4], SEL);
  nand nand_11 (nand_11_out, A[4], nand_1_out);
  nand nand_12 (nand_12_out, B[5], SEL);
  nand nand_13 (nand_13_out, A[5], nand_1_out);
  nand nand_14 (nand_14_out, B[6], SEL);
  nand nand_15 (nand_15_out, A[6], nand_1_out);
  nand nand_16 (nand_16_out, B[7], SEL);
  nand nand_17 (nand_17_out, A[7], nand_1_out);
  nand nand_18 (OUT[0], nand_2_out, nand_3_out);
  nand nand_19 (OUT[1], nand_4_out, nand_5_out);
  nand nand_20 (OUT[2], nand_6_out, nand_7_out);
  nand nand_21 (OUT[3], nand_8_out, nand_9_out);
  nand nand_22 (OUT[4], nand_10_out, nand_11_out);
  nand nand_23 (OUT[5], nand_12_out, nand_13_out);
  nand nand_24 (OUT[6], nand_14_out, nand_15_out);
  nand nand_25 (OUT[7], nand_16_out, nand_17_out);
endmodule
