// Digital circuit 3bit_johnson_counter.dig as structural Verilog
module _3bit_johnson_counter (
  input  CLK,
  input  RST,
  output [2:0] OUTPUT
);

  wire nand_1_out, nand_2_out, nand_3_out, nand_4_out, nand_5_out, nand_6_out, nand_7_out, nand_8_out,
       nand_9_out, nand_10_out, nand_11_out, nand_12_out, nand_13_out, nand_14_out, nand_15_out, nand_16_out,
       nand_17_out, nand_18_out, nand_19_out, nand_20_out, nand_21_out, nand_22_out, nand_23_out,
       nand_24_out, nand_25_out, nand_26_out, nand_27_out, nand_28_out, nand_29_out, nand_31_out,
       nand_33_out, nand_35_out;

  nand nand_1 (nand_1_out, CLK, CLK);
  nand nand_2 (nand_2_out, OUTPUT[2], OUTPUT[2]);
  nand nand_3 (nand_3_out, OUTPUT[0], OUTPUT[0]);
  nand nand_4 (nand_4_out, OUTPUT[1], OUTPUT[1]);
  nand nand_5 (nand_5_out, nand_1_out, nand_1_out);
  nand nand_6 (nand_6_out, OUTPUT[2], nand_1_out);
  nand nand_7 (nand_7_out, nand_1_out, nand_2_out);
  nand nand_8 (nand_8_out, OUTPUT[0], nand_1_out);
  nand nand_9 (nand_9_out, nand_1_out, nand_3_out);
  nand nand_10 (nand_10_out, OUTPUT[1], nand_1_out);
  nand nand_11 (nand_11_out, nand_1_out, nand_4_out);
  nand nand_12 (nand_12_out, nand_6_out, nand_13_out);
  nand nand_13 (nand_13_out, nand_12_out, nand_7_out);
  nand nand_14 (nand_14_out, nand_8_out, nand_15_out);
  nand nand_15 (nand_15_out, nand_14_out, nand_9_out);
  nand nand_16 (nand_16_out, nand_10_out, nand_17_out);
  nand nand_17 (nand_17_out, nand_16_out, nand_11_out);
  nand nand_18 (nand_18_out, nand_5_out, nand_12_out);
  nand nand_19 (nand_19_out, nand_13_out, nand_5_out);
  nand nand_20 (nand_20_out, nand_5_out, nand_14_out);
  nand nand_21 (nand_21_out, nand_15_out, nand_5_out);
  nand nand_22 (nand_22_out, nand_5_out, nand_16_out);
  nand nand_23 (nand_23_out, nand_17_out, nand_5_out);
  nand nand_24 (nand_24_out, nand_18_out, RST);
  nand nand_25 (nand_25_out, nand_21_out, RST);
  nand nand_26 (nand_26_out, nand_23_out, RST);
  nand nand_27 (nand_27_out, nand_24_out, nand_24_out);
  nand nand_28 (nand_28_out, nand_25_out, nand_25_out);
  nand nand_29 (nand_29_out, nand_26_out, nand_26_out);
  nand nand_30 (OUTPUT[0], nand_27_out, nand_31_out);
  nand nand_31 (nand_31_out, OUTPUT[0], nand_19_out);
  nand nand_32 (OUTPUT[1], nand_20_out, nand_33_out);
  nand nand_33 (nand_33_out, OUTPUT[1], nand_28_out);
  nand nand_34 (OUTPUT[2], nand_22_out, nand_35_out);
  nand nand_35 (nand_35_out, OUTPUT[2], nand_29_out);
endmodule
