// Digital circuit 4bit_johnson_counter.dig as structural Verilog
module _4bit_johnson_counter (
  input  CLK,
  input  RST,
  output [3:0] OUTPUT
);

  wire nand_1_out, nand_2_out, nand_3_out, nand_4_out, nand_5_out, nand_6_out, nand_7_out, nand_8_out,
       nand_9_out, nand_10_out, nand_11_out, nand_12_out, nand_13_out, nand_14_out, nand_15_out, nand_16_out,
       nand_17_out, nand_18_out, nand_19_out, nand_20_out, nand_21_out, nand_22_out, nand_23_out,
       nand_24_out, nand_25_out, nand_26_out, nand_27_out, nand_28_out, nand_29_out, nand_30_out,
       nand_31_out, nand_32_out, nand_33_out, nand_34_out, nand_35_out, nand_36_out, nand_37_out,
       nand_38_out, nand_40_out, nand_42_out, nand_44_out, nand_46_out;

  nand nand_1 (nand_1_out, CLK, CLK);
  nand nand_2 (nand_2_out, OUTPUT[3], OUTPUT[3]);
  nand nand_3 (nand_3_out, OUTPUT[0], OUTPUT[0]);
  nand nand_4 (nand_4_out, OUTPUT[1], OUTPUT[1]);
  nand nand_5 (nand_5_out, OUTPUT[2], OUTPUT[2]);
  nand nand_6 (nand_6_out, nand_1_out, nand_1_out);
  nand nand_7 (nand_7_out, OUTPUT[3], nand_1_out);
  nand nand_8 (nand_8_out, nand_1_out, nand_2_out);
  nand nand_9 (nand_9_out, OUTPUT[0], nand_1_out);
  nand nand_10 (nand_10_out, nand_1_out, nand_3_out);
  nand nand_11 (nand_11_out, OUTPUT[1], nand_1_out);
  nand nand_12 (nand_12_out, nand_1_out, nand_4_out);
  nand nand_13 (nand_13_out, OUTPUT[2], nand_1_out);
  nand nand_14 (nand_14_out, nand_1_out, nand_5_out);
  nand nand_15 (nand_15_out, nand_7_out, nand_16_out);
  nand nand_16 (nand_16_out, nand_15_out, nand_8_out);
  nand nand_17 (nand_17_out, nand_9_out, nand_18_out);
  nand nand_18 (nand_18_out, nand_17_out, nand_10_out);
  nand nand_19 (nand_19_out, nand_11_out, nand_20_out);
  nand nand_20 (nand_20_out, nand_19_out, nand_12_out);
  nand nand_21 (nand_21_out, nand_13_out, nand_22_out);
  nand nand_22 (nand_22_out, nand_21_out, nand_14_out);
  nand nand_23 (nand_23_out, nand_6_out, nand_15_out);
  nand nand_24 (nand_24_out, nand_16_out, nand_6_out);
  nand nand_25 (nand_25_out, nand_6_out, nand_17_out);
  nand nand_26 (nand_26_out, nand_18_out, nand_6_out);
  nand nand_27 (nand_27_out, nand_6_out, nand_19_out);
  nand nand_28 (nand_28_out, nand_20_out, nand_6_out);
  nand nand_29 (nand_29_out, nand_6_out, nand_21_out);
  nand nand_30 (nand_30_out, nand_22_out, nand_6_out);
  nand nand_31 (nand_31_out, nand_23_out, RST);
  nand nand_32 (nand_32_out, nand_26_out, RST);
  nand nand_33 (nand_33_out, nand_28_out, RST);
  nand nand_34 (nand_34_out, nand_30_out, RST);
  nand nand_35 (nand_35_out, nand_31_out, nand_31_out);
  nand nand_36 (nand_36_out, nand_32_out, nand_32_out);
  nand nand_37 (nand_37_out, nand_33_out, nand_33_out);
  nand nand_38 (nand_38_out, nand_34_out, nand_34_out);
  nand nand_39 (OUTPUT[0], nand_35_out, nand_40_out);
  nand nand_40 (nand_40_out, OUTPUT[0], nand_24_out);
  nand nand_41 (OUTPUT[1], nand_25_out, nand_42_out);
  nand nand_42 (nand_42_out, OUTPUT[1], nand_36_out);
  nand nand_43 (OUTPUT[2], nand_27_out, nand_44_out);
  nand nand_44 (nand_44_out, OUTPUT[2], nand_37_out);
  nand nand_45 (OUTPUT[3], nand_29_out, nand_46_out);
  nand nand_46 (nand_46_out, OUTPUT[3], nand_38_out);
endmodule
