// Digital circuit 4bit_masked_or.dig as structural Verilog
module _4bit_masked_or (
  input  [3:0] DATA,
  input  [3:0] MASK,
  output OUT
);

  wire nand_1_out, nand_2_out, nand_3_out, nand_4_out, nand_5_out, nand_6_out, nand_7_out, nand_8_out;

  nand nand_1 (nand_1_out, DATA[0], MASK[0]);
  nand nand_2 (nand_2_out, DATA[1], MASK[1]);
  nand nand_3 (nand_3_out, DATA[2], MASK[2]);
  nand nand_4 (nand_4_out, DATA[3], MASK[3]);
  nand nand_5 (nand_5_out, nand_1_out, nand_1_out);
  nand nand_6 (nand_6_out, nand_2_out, nand_2_out);
  nand nand_7 (nand_7_out, nand_3_out, nand_3_out);
  nand nand_8 (nand_8_out, nand_4_out, nand_4_out);
  or or_1 (OUT, nand_5_out, nand_6_out, nand_7_out, nand_8_out);

  // Notes on the sheet:
  //   Schottky OR
endmodule
