// Digital circuit 4x16bit_interleave.dig as structural Verilog
module _4x16bit_interleave (
  input  [15:0] WORD0,
  input  [15:0] WORD1,
  input  [15:0] WORD2,
  input  [15:0] WORD3,
  output [3:0] OUT0,
  output [3:0] OUT1,
  output [3:0] OUT2,
  output [3:0] OUT3,
  output [3:0] OUT4,
  output [3:0] OUT5,
  output [3:0] OUT6,
  output [3:0] OUT7,
  output [3:0] OUT8,
  output [3:0] OUT9,
  output [3:0] OUT10,
  output [3:0] OUT11,
  output [3:0] OUT12,
  output [3:0] OUT13,
  output [3:0] OUT14,
  output [3:0] OUT15
);


  assign OUT0 = {WORD3[0], WORD2[0], WORD1[0], WORD0[0]};
  assign OUT1 = {WORD3[1], WORD2[1], WORD1[1], WORD0[1]};
  assign OUT2 = {WORD3[2], WORD2[2], WORD1[2], WORD0[2]};
  assign OUT3 = {WORD3[3], WORD2[3], WORD1[3], WORD0[3]};
  assign OUT4 = {WORD3[4], WORD2[4], WORD1[4], WORD0[4]};
  assign OUT5 = {WORD3[5], WORD2[5], WORD1[5], WORD0[5]};
  assign OUT6 = {WORD3[6], WORD2[6], WORD1[6], WORD0[6]};
  assign OUT7 = {WORD3[7], WORD2[7], WORD1[7], WORD0[7]};
  assign OUT8 = {WORD3[8], WORD2[8], WORD1[8], WORD0[8]};
  assign OUT9 = {WORD3[9], WORD2[9], WORD1[9], WORD0[9]};
  assign OUT10 = {WORD3[10], WORD2[10], WORD1[10], WORD0[10]};
  assign OUT11 = {WORD3[11], WORD2[11], WORD1[11], WORD0[11]};
  assign OUT12 = {WORD3[12], WORD2[12], WORD1[12], WORD0[12]};
  assign OUT13 = {WORD3[13], WORD2[13], WORD1[13], WORD0[13]};
  assign OUT14 = {WORD3[14], WORD2[14], WORD1[14], WORD0[14]};
  assign OUT15 = {WORD3[15], WORD2[15], WORD1[15], WORD0[15]};
endmodule
