// Digital circuit 4x8bit_masked_or.dig as structural Verilog
module _4x8bit_masked_or (
  input  [1:0] SELECT,
  input  [3:0] DATA0,
  input  [3:0] DATA1,
  input  [3:0] DATA2,
  input  [3:0] DATA3,
  input  [3:0] DATA4,
  input  [3:0] DATA5,
  input  [3:0] DATA6,
  input  [3:0] DATA7,
  output OUT0,
  output OUT1,
  output OUT2,
  output OUT3,
  output OUT4,
  output OUT5,
  output OUT6,
  output OUT7
);

  wire [3:0] _2bit_decode_1_out;

  _2bit_decode _2bit_decode_1 (.IN(SELECT), .OUT(_2bit_decode_1_out));
  _4bit_masked_or _4bit_masked_or_1 (.DATA(DATA0), .MASK(_2bit_decode_1_out), .OUT(OUT0));
  _4bit_masked_or _4bit_masked_or_2 (.DATA(DATA1), .MASK(_2bit_decode_1_out), .OUT(OUT1));
  _4bit_masked_or _4bit_masked_or_3 (.DATA(DATA2), .MASK(_2bit_decode_1_out), .OUT(OUT2));
  _4bit_masked_or _4bit_masked_or_4 (.DATA(DATA3), .MASK(_2bit_decode_1_out), .OUT(OUT3));
  _4bit_masked_or _4bit_masked_or_5 (.DATA(DATA4), .MASK(_2bit_decode_1_out), .OUT(OUT4));
  _4bit_masked_or _4bit_masked_or_6 (.DATA(DATA5), .MASK(_2bit_decode_1_out), .OUT(OUT5));
  _4bit_masked_or _4bit_masked_or_7 (.DATA(DATA6), .MASK(_2bit_decode_1_out), .OUT(OUT6));
  _4bit_masked_or _4bit_masked_or_8 (.DATA(DATA7), .MASK(_2bit_decode_1_out), .OUT(OUT7));
endmodule
