// Digital circuit 4x8bit_register_file_async_clear.dig as structural Verilog
module _4x8bit_register_file_async_clear (
  input  CLK,
  input  CLR,
  input  [1:0] WSEL,
  input  [1:0] R1SEL,
  input  [1:0] R2SEL,
  input  WEN,
  input  [7:0] WRITE,
  output [7:0] READ1,
  output [7:0] READ2
);

  wire nand_1_out, nand_2_out, nand_3_out, nand_4_out, nand_5_out, nand_6_out, nand_7_out, nand_8_out,
       select2_3_o0, select2_3_o1, select2_3_o2, select2_3_o3;
  wire [3:0] _4x8bit_interleave_1_out0, _4x8bit_interleave_1_out1, _4x8bit_interleave_1_out2,
       _4x8bit_interleave_1_out3, _4x8bit_interleave_1_out4, _4x8bit_interleave_1_out5,
       _4x8bit_interleave_1_out6, _4x8bit_interleave_1_out7, select2_1_o3, select2_2_o1;
  wire [7:0] _8bit_register_async_clear_1_read, _8bit_register_async_clear_2_read,
       _8bit_register_async_clear_3_read, _8bit_register_async_clear_4_read;

  select2 select2_1 (
    .S0(R1SEL[0]), .S1(R1SEL[1]), .O0(select2_1_o3[0]), .O1(select2_1_o3[1]), .O2(select2_1_o3[2]),
    .O3(select2_1_o3[3]));
  select2 select2_2 (
    .S0(R2SEL[0]), .S1(R2SEL[1]), .O0(select2_2_o1[0]), .O1(select2_2_o1[1]), .O2(select2_2_o1[2]),
    .O3(select2_2_o1[3]));
  select2 select2_3 (
    .S0(WSEL[0]), .S1(WSEL[1]), .O0(select2_3_o0), .O1(select2_3_o1), .O2(select2_3_o2), .O3(select2_3_o3));
  nand nand_1 (nand_1_out, WEN, select2_3_o0);
  nand nand_2 (nand_2_out, WEN, select2_3_o1);
  nand nand_3 (nand_3_out, WEN, select2_3_o2);
  nand nand_4 (nand_4_out, WEN, select2_3_o3);
  nand nand_5 (nand_5_out, nand_1_out, nand_1_out);
  nand nand_6 (nand_6_out, nand_2_out, nand_2_out);
  nand nand_7 (nand_7_out, nand_3_out, nand_3_out);
  nand nand_8 (nand_8_out, nand_4_out, nand_4_out);
  deselect2 deselect2_1 (.BI(_4x8bit_interleave_1_out0), .AI(select2_1_o3), .O(READ1[0]));
  deselect2 deselect2_2 (.BI(_4x8bit_interleave_1_out0), .AI(select2_2_o1), .O(READ2[0]));
  _8bit_register_async_clear _8bit_register_async_clear_1 (
    .CLK(CLK), .WEN(nand_5_out), .WRITE(WRITE), .CLR(CLR), .READ(_8bit_register_async_clear_1_read));
  _8bit_register_async_clear _8bit_register_async_clear_2 (
    .CLK(CLK), .WEN(nand_6_out), .WRITE(WRITE), .CLR(CLR), .READ(_8bit_register_async_clear_2_read));
  _8bit_register_async_clear _8bit_register_async_clear_3 (
    .CLK(CLK), .WEN(nand_7_out), .WRITE(WRITE), .CLR(CLR), .READ(_8bit_register_async_clear_3_read));
  _8bit_register_async_clear _8bit_register_async_clear_4 (
    .CLK(CLK), .WEN(nand_8_out), .WRITE(WRITE), .CLR(CLR), .READ(_8bit_register_async_clear_4_read));
  deselect2 deselect2_3 (.BI(_4x8bit_interleave_1_out1), .AI(select2_1_o3), .O(READ1[1]));
  deselect2 deselect2_4 (.BI(_4x8bit_interleave_1_out1), .AI(select2_2_o1), .O(READ2[1]));
  deselect2 deselect2_5 (.BI(_4x8bit_interleave_1_out2), .AI(select2_1_o3), .O(READ1[2]));
  deselect2 deselect2_6 (.BI(_4x8bit_interleave_1_out2), .AI(select2_2_o1), .O(READ2[2]));
  deselect2 deselect2_7 (.BI(_4x8bit_interleave_1_out3), .AI(select2_1_o3), .O(READ1[3]));
  deselect2 deselect2_8 (.BI(_4x8bit_interleave_1_out3), .AI(select2_2_o1), .O(READ2[3]));
  _4x8bit_interleave _4x8bit_interleave_1 (
    .WORD0(_8bit_register_async_clear_1_read), .WORD1(_8bit_register_async_clear_2_read),
    .WORD2(_8bit_register_async_clear_3_read), .WORD3(_8bit_register_async_clear_4_read),
    .OUT0(_4x8bit_interleave_1_out0), .OUT1(_4x8bit_interleave_1_out1), .OUT2(_4x8bit_interleave_1_out2),
    .OUT3(_4x8bit_interleave_1_out3), .OUT4(_4x8bit_interleave_1_out4), .OUT5(_4x8bit_interleave_1_out5),
    .OUT6(_4x8bit_interleave_1_out6), .OUT7(_4x8bit_interleave_1_out7));
  deselect2 deselect2_9 (.BI(_4x8bit_interleave_1_out4), .AI(select2_1_o3), .O(READ1[4]));
  deselect2 deselect2_10 (.BI(_4x8bit_interleave_1_out4), .AI(select2_2_o1), .O(READ2[4]));
  deselect2 deselect2_11 (.BI(_4x8bit_interleave_1_out5), .AI(select2_1_o3), .O(READ1[5]));
  deselect2 deselect2_12 (.BI(_4x8bit_interleave_1_out5), .AI(select2_2_o1), .O(READ2[5]));
  deselect2 deselect2_13 (.BI(_4x8bit_interleave_1_out6), .AI(select2_1_o3), .O(READ1[6]));
  deselect2 deselect2_14 (.BI(_4x8bit_interleave_1_out6), .AI(select2_2_o1), .O(READ2[6]));
  deselect2 deselect2_15 (.BI(_4x8bit_interleave_1_out7), .AI(select2_1_o3), .O(READ1[7]));
  deselect2 deselect2_16 (.BI(_4x8bit_interleave_1_out7), .AI(select2_2_o1), .O(READ2[7]));
endmodule
