// Digital circuit 8bit_add_sub.dig as structural Verilog
module _8bit_add_sub (
  input  [7:0] A,
  input  [7:0] B,
  input  ADD_SUB,
  input  CIN,
  output [7:0] RESULT,
  output COUT,
  output OVERFLOW
);

  wire full_adder_1_cout, full_adder_2_cout, full_adder_3_cout, full_adder_4_cout, full_adder_5_cout,
       full_adder_6_cout, full_adder_7_cout, full_adder_8_cout, nand_1_out, nand_2_out, nand_3_out,
       nand_4_out, nand_5_out, nand_6_out, nand_7_out, nand_8_out, nand_9_out, nand_10_out, nand_11_out,
       nand_12_out, nand_13_out, nand_14_out, nand_15_out, nand_16_out, nand_17_out, nand_18_out,
       nand_19_out, nand_20_out, nand_21_out, nand_22_out, nand_23_out, nand_24_out, nand_25_out,
       nand_26_out, nand_27_out, nand_28_out, nand_29_out, nand_30_out, nand_31_out, nand_32_out,
       nand_33_out, nand_34_out, nand_35_out, nand_36_out, nand_37_out, nand_38_out, nand_39_out,
       nand_40_out, nand_41_out, nand_42_out;

  nand nand_1 (nand_1_out, B[0], ADD_SUB);
  nand nand_2 (nand_2_out, B[1], ADD_SUB);
  nand nand_3 (nand_3_out, B[2], ADD_SUB);
  nand nand_4 (nand_4_out, B[3], ADD_SUB);
  nand nand_5 (nand_5_out, B[4], ADD_SUB);
  nand nand_6 (nand_6_out, B[5], ADD_SUB);
  nand nand_7 (nand_7_out, B[6], ADD_SUB);
  nand nand_8 (nand_8_out, B[7], ADD_SUB);
  nand nand_9 (nand_9_out, B[0], nand_1_out);
  nand nand_10 (nand_10_out, nand_1_out, ADD_SUB);
  nand nand_11 (nand_11_out, B[1], nand_2_out);
  nand nand_12 (nand_12_out, nand_2_out, ADD_SUB);
  nand nand_13 (nand_13_out, B[2], nand_3_out);
  nand nand_14 (nand_14_out, nand_3_out, ADD_SUB);
  nand nand_15 (nand_15_out, B[3], nand_4_out);
  nand nand_16 (nand_16_out, nand_4_out, ADD_SUB);
  nand nand_17 (nand_17_out, B[4], nand_5_out);
  nand nand_18 (nand_18_out, nand_5_out, ADD_SUB);
  nand nand_19 (nand_19_out, B[5], nand_6_out);
  nand nand_20 (nand_20_out, nand_6_out, ADD_SUB);
  nand nand_21 (nand_21_out, B[6], nand_7_out);
  nand nand_22 (nand_22_out, nand_7_out, ADD_SUB);
  nand nand_23 (nand_23_out, B[7], nand_8_out);
  nand nand_24 (nand_24_out, nand_8_out, ADD_SUB);
  nand nand_25 (nand_25_out, CIN, ADD_SUB);
  nand nand_26 (nand_26_out, nand_9_out, nand_10_out);
  nand nand_27 (nand_27_out, nand_11_out, nand_12_out);
  nand nand_28 (nand_28_out, nand_13_out, nand_14_out);
  nand nand_29 (nand_29_out, nand_15_out, nand_16_out);
  nand nand_30 (nand_30_out, nand_17_out, nand_18_out);
  nand nand_31 (nand_31_out, nand_19_out, nand_20_out);
  nand nand_32 (nand_32_out, nand_21_out, nand_22_out);
  nand nand_33 (nand_33_out, nand_23_out, nand_24_out);
  nand nand_34 (nand_34_out, CIN, nand_25_out);
  nand nand_35 (nand_35_out, nand_25_out, ADD_SUB);
  nand nand_36 (nand_36_out, nand_34_out, nand_35_out);
  full_adder full_adder_1 (.A(A[0]), .B(nand_26_out), .CIN(nand_36_out), .S(RESULT[0]), .COUT(full_adder_1_cout));
  full_adder full_adder_2 (.A(A[1]), .B(nand_27_out), .CIN(full_adder_1_cout), .S(RESULT[1]), .COUT(full_adder_2_cout));
  full_adder full_adder_3 (.A(A[2]), .B(nand_28_out), .CIN(full_adder_2_cout), .S(RESULT[2]), .COUT(full_adder_3_cout));
  full_adder full_adder_4 (.A(A[3]), .B(nand_29_out), .CIN(full_adder_3_cout), .S(RESULT[3]), .COUT(full_adder_4_cout));
  full_adder full_adder_5 (.A(A[4]), .B(nand_30_out), .CIN(full_adder_4_cout), .S(RESULT[4]), .COUT(full_adder_5_cout));
  full_adder full_adder_6 (.A(A[5]), .B(nand_31_out), .CIN(full_adder_5_cout), .S(RESULT[5]), .COUT(full_adder_6_cout));
  full_adder full_adder_7 (.A(A[6]), .B(nand_32_out), .CIN(full_adder_6_cout), .S(RESULT[6]), .COUT(full_adder_7_cout));
  full_adder full_adder_8 (.A(A[7]), .B(nand_33_out), .CIN(full_adder_7_cout), .S(RESULT[7]), .COUT(full_adder_8_cout));
  nand nand_37 (nand_37_out, full_adder_8_cout, ADD_SUB);
  nand nand_38 (nand_38_out, full_adder_8_cout, full_adder_7_cout);
  nand nand_39 (nand_39_out, full_adder_8_cout, nand_37_out);
  nand nand_40 (nand_40_out, nand_37_out, ADD_SUB);
  nand nand_41 (nand_41_out, full_adder_8_cout, nand_38_out);
  nand nand_42 (nand_42_out, nand_38_out, full_adder_7_cout);
  nand nand_43 (COUT, nand_39_out, nand_40_out);
  nand nand_44 (OVERFLOW, nand_41_out, nand_42_out);
endmodule
