// Digital circuit 8bit_individual_mux.dig as structural Verilog
module _8bit_individual_mux (
  input  [7:0] SEL,
  input  [7:0] A,
  input  [7:0] B,
  output [7:0] OUT
);

  _2bit_mux _2bit_mux_1 (.S(SEL[0]), .A(A[0]), .B(B[0]), .OUT(OUT[0]));
  _2bit_mux _2bit_mux_2 (.S(SEL[1]), .A(A[1]), .B(B[1]), .OUT(OUT[1]));
  _2bit_mux _2bit_mux_3 (.S(SEL[2]), .A(A[2]), .B(B[2]), .OUT(OUT[2]));
  _2bit_mux _2bit_mux_4 (.S(SEL[3]), .A(A[3]), .B(B[3]), .OUT(OUT[3]));
  _2bit_mux _2bit_mux_5 (.S(SEL[4]), .A(A[4]), .B(B[4]), .OUT(OUT[4]));
  _2bit_mux _2bit_mux_6 (.S(SEL[5]), .A(A[5]), .B(B[5]), .OUT(OUT[5]));
  _2bit_mux _2bit_mux_7 (.S(SEL[6]), .A(A[6]), .B(B[6]), .OUT(OUT[6]));
  _2bit_mux _2bit_mux_8 (.S(SEL[7]), .A(A[7]), .B(B[7]), .OUT(OUT[7]));
endmodule
