// Digital circuit 8bit_mask.dig as structural Verilog
module _8bit_mask (
  input  [7:0] DATA,
  input  [7:0] MASK,
  output [7:0] OUT
);

  wire nand_1_out, nand_2_out, nand_3_out, nand_4_out, nand_5_out, nand_6_out, nand_7_out, nand_8_out;

  nand nand_1 (nand_1_out, DATA[0], MASK[0]);
  nand nand_2 (nand_2_out, DATA[1], MASK[1]);
  nand nand_3 (nand_3_out, DATA[2], MASK[2]);
  nand nand_4 (nand_4_out, DATA[3], MASK[3]);
  nand nand_5 (nand_5_out, DATA[4], MASK[4]);
  nand nand_6 (nand_6_out, DATA[5], MASK[5]);
  nand nand_7 (nand_7_out, DATA[6], MASK[6]);
  nand nand_8 (nand_8_out, MASK[7], DATA[7]);
  nand nand_9 (OUT[0], nand_1_out, nand_1_out);
  nand nand_10 (OUT[1], nand_2_out, nand_2_out);
  nand nand_11 (OUT[2], nand_3_out, nand_3_out);
  nand nand_12 (OUT[3], nand_4_out, nand_4_out);
  nand nand_13 (OUT[4], nand_5_out, nand_5_out);
  nand nand_14 (OUT[5], nand_6_out, nand_6_out);
  nand nand_15 (OUT[6], nand_7_out, nand_7_out);
  nand nand_16 (OUT[7], nand_8_out, nand_8_out);
endmodule
