// Digital circuit 8bit_register_individual_write_flags.dig as structural Verilog
module _8bit_register_individual_write_flags (
  input  CLK,
  input  WEN,
  input  [7:0] WRITE,
  input  CLR,
  output [7:0] READ
);

  wire nand_1_out, nand_2_out, nand_3_out, nand_4_out, nand_5_out, nand_6_out, nand_7_out, nand_8_out,
       nand_9_out, nand_10_out, nand_11_out, nand_12_out, nand_13_out, nand_14_out, nand_15_out, nand_16_out,
       nand_17_out, nand_18_out, nand_19_out, nand_20_out, nand_21_out, nand_22_out, nand_23_out,
       nand_24_out, nand_25_out, nand_26_out, nand_27_out, nand_28_out, nand_29_out, nand_30_out,
       nand_31_out, nand_32_out, nand_33_out, nand_34_out, nand_35_out, nand_36_out, nand_37_out,
       nand_38_out, nand_39_out, nand_40_out, nand_41_out, nand_42_out, nand_43_out, nand_44_out,
       nand_45_out, nand_46_out, nand_47_out, nand_48_out, nand_49_out, nand_50_out, nand_51_out,
       nand_52_out, nand_53_out, nand_54_out, nand_55_out, nand_56_out, nand_57_out, nand_58_out,
       nand_59_out, nand_60_out, nand_61_out, nand_62_out, nand_63_out, nand_64_out, nand_65_out,
       nand_66_out, nand_67_out, nand_68_out, nand_69_out, nand_70_out, nand_71_out, nand_72_out,
       nand_73_out, nand_74_out, nand_75_out, nand_76_out, nand_78_out, nand_80_out, nand_82_out,
       nand_84_out, nand_86_out, nand_88_out, nand_90_out, nand_92_out;

  nand nand_1 (nand_1_out, CLR, WEN);
  nand nand_2 (nand_2_out, nand_1_out, nand_1_out);
  nand nand_3 (nand_3_out, nand_2_out, CLK);
  nand nand_4 (nand_4_out, WRITE[0], WRITE[0]);
  nand nand_5 (nand_5_out, WRITE[1], WRITE[1]);
  nand nand_6 (nand_6_out, WRITE[2], WRITE[2]);
  nand nand_7 (nand_7_out, WRITE[3], WRITE[3]);
  nand nand_8 (nand_8_out, WRITE[4], WRITE[4]);
  nand nand_9 (nand_9_out, WRITE[5], WRITE[5]);
  nand nand_10 (nand_10_out, WRITE[6], WRITE[6]);
  nand nand_11 (nand_11_out, WRITE[7], WRITE[7]);
  nand nand_12 (nand_12_out, nand_3_out, nand_3_out);
  nand nand_13 (nand_13_out, WRITE[0], nand_3_out);
  nand nand_14 (nand_14_out, nand_3_out, nand_4_out);
  nand nand_15 (nand_15_out, WRITE[1], nand_3_out);
  nand nand_16 (nand_16_out, nand_3_out, nand_5_out);
  nand nand_17 (nand_17_out, WRITE[2], nand_3_out);
  nand nand_18 (nand_18_out, nand_3_out, nand_6_out);
  nand nand_19 (nand_19_out, WRITE[3], nand_3_out);
  nand nand_20 (nand_20_out, nand_3_out, nand_7_out);
  nand nand_21 (nand_21_out, WRITE[4], nand_3_out);
  nand nand_22 (nand_22_out, nand_3_out, nand_8_out);
  nand nand_23 (nand_23_out, WRITE[5], nand_3_out);
  nand nand_24 (nand_24_out, nand_3_out, nand_9_out);
  nand nand_25 (nand_25_out, WRITE[6], nand_3_out);
  nand nand_26 (nand_26_out, nand_3_out, nand_10_out);
  nand nand_27 (nand_27_out, WRITE[7], nand_3_out);
  nand nand_28 (nand_28_out, nand_3_out, nand_11_out);
  nand nand_29 (nand_29_out, nand_13_out, nand_30_out);
  nand nand_30 (nand_30_out, nand_29_out, nand_14_out);
  nand nand_31 (nand_31_out, nand_15_out, nand_32_out);
  nand nand_32 (nand_32_out, nand_31_out, nand_16_out);
  nand nand_33 (nand_33_out, nand_17_out, nand_34_out);
  nand nand_34 (nand_34_out, nand_33_out, nand_18_out);
  nand nand_35 (nand_35_out, nand_19_out, nand_36_out);
  nand nand_36 (nand_36_out, nand_35_out, nand_20_out);
  nand nand_37 (nand_37_out, nand_21_out, nand_38_out);
  nand nand_38 (nand_38_out, nand_37_out, nand_22_out);
  nand nand_39 (nand_39_out, nand_23_out, nand_40_out);
  nand nand_40 (nand_40_out, nand_39_out, nand_24_out);
  nand nand_41 (nand_41_out, nand_25_out, nand_42_out);
  nand nand_42 (nand_42_out, nand_41_out, nand_26_out);
  nand nand_43 (nand_43_out, nand_27_out, nand_44_out);
  nand nand_44 (nand_44_out, nand_43_out, nand_28_out);
  nand nand_45 (nand_45_out, nand_12_out, nand_29_out);
  nand nand_46 (nand_46_out, nand_30_out, nand_12_out);
  nand nand_47 (nand_47_out, nand_12_out, nand_31_out);
  nand nand_48 (nand_48_out, nand_32_out, nand_12_out);
  nand nand_49 (nand_49_out, nand_12_out, nand_33_out);
  nand nand_50 (nand_50_out, nand_34_out, nand_12_out);
  nand nand_51 (nand_51_out, nand_12_out, nand_35_out);
  nand nand_52 (nand_52_out, nand_36_out, nand_12_out);
  nand nand_53 (nand_53_out, nand_12_out, nand_37_out);
  nand nand_54 (nand_54_out, nand_38_out, nand_12_out);
  nand nand_55 (nand_55_out, nand_12_out, nand_39_out);
  nand nand_56 (nand_56_out, nand_40_out, nand_12_out);
  nand nand_57 (nand_57_out, nand_12_out, nand_41_out);
  nand nand_58 (nand_58_out, nand_42_out, nand_12_out);
  nand nand_59 (nand_59_out, nand_12_out, nand_43_out);
  nand nand_60 (nand_60_out, nand_44_out, nand_12_out);
  nand nand_61 (nand_61_out, nand_46_out, CLR);
  nand nand_62 (nand_62_out, nand_48_out, CLR);
  nand nand_63 (nand_63_out, nand_50_out, CLR);
  nand nand_64 (nand_64_out, nand_52_out, CLR);
  nand nand_65 (nand_65_out, nand_54_out, CLR);
  nand nand_66 (nand_66_out, nand_56_out, CLR);
  nand nand_67 (nand_67_out, nand_58_out, CLR);
  nand nand_68 (nand_68_out, nand_60_out, CLR);
  nand nand_69 (nand_69_out, nand_61_out, nand_61_out);
  nand nand_70 (nand_70_out, nand_62_out, nand_62_out);
  nand nand_71 (nand_71_out, nand_63_out, nand_63_out);
  nand nand_72 (nand_72_out, nand_64_out, nand_64_out);
  nand nand_73 (nand_73_out, nand_65_out, nand_65_out);
  nand nand_74 (nand_74_out, nand_66_out, nand_66_out);
  nand nand_75 (nand_75_out, nand_67_out, nand_67_out);
  nand nand_76 (nand_76_out, nand_68_out, nand_68_out);
  nand nand_77 (READ[0], nand_45_out, nand_78_out);
  nand nand_78 (nand_78_out, READ[0], nand_69_out);
  nand nand_79 (READ[1], nand_47_out, nand_80_out);
  nand nand_80 (nand_80_out, READ[1], nand_70_out);
  nand nand_81 (READ[2], nand_49_out, nand_82_out);
  nand nand_82 (nand_82_out, READ[2], nand_71_out);
  nand nand_83 (READ[3], nand_51_out, nand_84_out);
  nand nand_84 (nand_84_out, READ[3], nand_72_out);
  nand nand_85 (READ[4], nand_53_out, nand_86_out);
  nand nand_86 (nand_86_out, READ[4], nand_73_out);
  nand nand_87 (READ[5], nand_55_out, nand_88_out);
  nand nand_88 (nand_88_out, READ[5], nand_74_out);
  nand nand_89 (READ[6], nand_57_out, nand_90_out);
  nand nand_90 (nand_90_out, READ[6], nand_75_out);
  nand nand_91 (READ[7], nand_59_out, nand_92_out);
  nand nand_92 (nand_92_out, READ[7], nand_76_out);
endmodule
