// Digital circuit 8bit_shifter.dig as structural Verilog
module _8bit_shifter (
  input  [7:0] A,
  input  [7:0] B,
  input  DIR,
  input  SIB,
  output [7:0] RESULT,
  output OUT
);

  wire [7:0] _2x8bit_mux_1_out, _2x8bit_mux_2_out, _2x8bit_mux_3_out, _2x8bit_mux_4_out, _2x8bit_mux_5_out,
       _2x8bit_mux_6_out;

  _2x8bit_mux _2x8bit_mux_1 (.SEL(B[0]), .B({A[6:0], SIB}), .A(A), .OUT(_2x8bit_mux_1_out));
  _2x8bit_mux _2x8bit_mux_2 (.SEL(B[0]), .B({SIB, A[7:1]}), .A(A), .OUT(_2x8bit_mux_2_out));
  _2bit_mux _2bit_mux_1 (.S(DIR), .A(A[7]), .B(A[0]), .OUT(OUT));
  _2x8bit_mux _2x8bit_mux_3 (
    .SEL(B[1]), .B({_2x8bit_mux_1_out[5:0], {2{SIB}}}), .A(_2x8bit_mux_1_out), .OUT(_2x8bit_mux_3_out));
  _2x8bit_mux _2x8bit_mux_4 (
    .SEL(B[1]), .B({{2{SIB}}, _2x8bit_mux_2_out[7:2]}), .A(_2x8bit_mux_2_out), .OUT(_2x8bit_mux_4_out));
  _2x8bit_mux _2x8bit_mux_5 (
    .SEL(B[2]), .B({_2x8bit_mux_3_out[3:0], {4{SIB}}}), .A(_2x8bit_mux_3_out), .OUT(_2x8bit_mux_5_out));
  _2x8bit_mux _2x8bit_mux_6 (
    .SEL(B[2]), .B({{4{SIB}}, _2x8bit_mux_4_out[7:4]}), .A(_2x8bit_mux_4_out), .OUT(_2x8bit_mux_6_out));
  _2x8bit_mux _2x8bit_mux_7 (.SEL(DIR), .B(_2x8bit_mux_6_out), .A(_2x8bit_mux_5_out), .OUT(RESULT));

  // Notes on the sheet:
  //   DIR: 0 = Shift Left
  //   1 = Shift Right
endmodule
