// Digital circuit 8x8bit_interleave.dig as structural Verilog
module _8x8bit_interleave (
  input  [7:0] WORD0,
  input  [7:0] WORD1,
  input  [7:0] WORD2,
  input  [7:0] WORD3,
  input  [7:0] WORD4,
  input  [7:0] WORD5,
  input  [7:0] WORD6,
  input  [7:0] WORD7,
  output [7:0] OUT0,
  output [7:0] OUT1,
  output [7:0] OUT2,
  output [7:0] OUT3,
  output [7:0] OUT4,
  output [7:0] OUT5,
  output [7:0] OUT6,
  output [7:0] OUT7
);


  assign OUT0 = {WORD7[0], WORD6[0], WORD5[0], WORD4[0], WORD3[0], WORD2[0], WORD1[0], WORD0[0]};
  assign OUT1 = {WORD7[1], WORD6[1], WORD5[1], WORD4[1], WORD3[1], WORD2[1], WORD1[1], WORD0[1]};
  assign OUT2 = {WORD7[2], WORD6[2], WORD5[2], WORD4[2], WORD3[2], WORD2[2], WORD1[2], WORD0[2]};
  assign OUT3 = {WORD7[3], WORD6[3], WORD5[3], WORD4[3], WORD3[3], WORD2[3], WORD1[3], WORD0[3]};
  assign OUT4 = {WORD7[4], WORD6[4], WORD5[4], WORD4[4], WORD3[4], WORD2[4], WORD1[4], WORD0[4]};
  assign OUT5 = {WORD7[5], WORD6[5], WORD5[5], WORD4[5], WORD3[5], WORD2[5], WORD1[5], WORD0[5]};
  assign OUT6 = {WORD7[6], WORD6[6], WORD5[6], WORD4[6], WORD3[6], WORD2[6], WORD1[6], WORD0[6]};
  assign OUT7 = {WORD7[7], WORD6[7], WORD5[7], WORD4[7], WORD3[7], WORD2[7], WORD1[7], WORD0[7]};
endmodule
