// Digital circuit clock.dig as structural Verilog
module clock (
  input  RESET,
  input  HALT,
  input  CONTINUE,
  input  CLKHALT,
  input  CLKIN,
  input  STEP,
  input  CLKEN,
  output ISHALTED,
  output RESET_2,
  output [2:0] CLOCKPHASE
);

  wire nand_1_out, nand_2_out, nand_3_out, nand_4_out, nand_5_out, nand_6_out, nand_7_out, nand_8_out,
       nand_9_out, nand_10_out, nand_13_out, nand_14_out, nand_15_out, nand_16_out, nand_17_out, nand_18_out;

  nand nand_1 (nand_1_out, CLKEN, CLKEN);
  nand nand_2 (nand_2_out, nand_1_out, STEP);
  nand nand_3 (nand_3_out, CLKEN, CLKIN);
  nand nand_4 (nand_4_out, nand_2_out, nand_3_out);
  nand nand_5 (nand_5_out, HALT, HALT);
  nand nand_6 (nand_6_out, RESET, RESET);
  nand nand_7 (nand_7_out, nand_16_out, nand_16_out);
  nand nand_8 (nand_8_out, nand_4_out, nand_4_out);
  nand nand_9 (nand_9_out, nand_5_out, nand_6_out);
  nand nand_10 (nand_10_out, nand_7_out, CONTINUE);
  nand nand_11 (RESET_2, RESET, RESET);
  nand nand_12 (ISHALTED, nand_7_out, nand_13_out);
  nand nand_13 (nand_13_out, ISHALTED, nand_10_out);
  nand nand_14 (nand_14_out, nand_9_out, nand_9_out);
  nand nand_15 (nand_15_out, nand_8_out, CLKHALT);
  nand nand_16 (nand_16_out, nand_14_out, nand_15_out);
  nand nand_17 (nand_17_out, nand_13_out, nand_4_out);
  nand nand_18 (nand_18_out, nand_17_out, nand_17_out);
  _3bit_johnson_counter _3bit_johnson_counter_1 (.CLK(nand_18_out), .RST(RESET_2), .OUTPUT(CLOCKPHASE));
endmodule
