// Digital circuit deselect3.dig as structural Verilog
module deselect3 (
  input  [7:0] BI,
  input  [7:0] AI,
  output O
);

  wire nand_1_out, nand_2_out, nand_3_out, nand_4_out, nand_5_out, nand_6_out, nand_7_out, nand_8_out,
       nand_9_out, nand_10_out, nand_11_out, nand_12_out, nand_13_out, nand_14_out, nand_15_out, nand_16_out,
       nand_17_out, nand_18_out, nand_19_out, nand_20_out;

  nand nand_1 (nand_1_out, AI[0], BI[0]);
  nand nand_2 (nand_2_out, AI[1], BI[1]);
  nand nand_3 (nand_3_out, AI[2], BI[2]);
  nand nand_4 (nand_4_out, AI[3], BI[3]);
  nand nand_5 (nand_5_out, AI[4], BI[4]);
  nand nand_6 (nand_6_out, AI[5], BI[5]);
  nand nand_7 (nand_7_out, AI[6], BI[6]);
  nand nand_8 (nand_8_out, AI[7], BI[7]);
  nand nand_9 (nand_9_out, nand_1_out, nand_2_out);
  nand nand_10 (nand_10_out, nand_3_out, nand_4_out);
  nand nand_11 (nand_11_out, nand_5_out, nand_6_out);
  nand nand_12 (nand_12_out, nand_7_out, nand_8_out);
  nand nand_13 (nand_13_out, nand_9_out, nand_9_out);
  nand nand_14 (nand_14_out, nand_10_out, nand_10_out);
  nand nand_15 (nand_15_out, nand_11_out, nand_11_out);
  nand nand_16 (nand_16_out, nand_12_out, nand_12_out);
  nand nand_17 (nand_17_out, nand_13_out, nand_14_out);
  nand nand_18 (nand_18_out, nand_15_out, nand_16_out);
  nand nand_19 (nand_19_out, nand_17_out, nand_17_out);
  nand nand_20 (nand_20_out, nand_18_out, nand_18_out);
  nand nand_21 (O, nand_19_out, nand_20_out);
endmodule
