// Digital circuit deselect4.dig as structural Verilog
module deselect4 (
  input  [15:0] BI,
  input  [15:0] AI,
  output OUT
);

  wire nand_1_out, nand_2_out, nand_3_out, nand_4_out, nand_5_out, nand_6_out, nand_7_out, nand_8_out,
       nand_9_out, nand_10_out, nand_11_out, nand_12_out, nand_13_out, nand_14_out, nand_15_out, nand_16_out,
       nand_17_out, nand_18_out, nand_19_out, nand_20_out, nand_21_out, nand_22_out, nand_23_out,
       nand_24_out, nand_25_out, nand_26_out, nand_27_out, nand_28_out, nand_29_out, nand_30_out,
       nand_31_out, nand_32_out;

  nand nand_1 (nand_1_out, AI[0], BI[0]);
  nand nand_2 (nand_2_out, AI[1], BI[1]);
  nand nand_3 (nand_3_out, AI[2], BI[2]);
  nand nand_4 (nand_4_out, AI[3], BI[3]);
  nand nand_5 (nand_5_out, AI[4], BI[4]);
  nand nand_6 (nand_6_out, AI[5], BI[5]);
  nand nand_7 (nand_7_out, AI[6], BI[6]);
  nand nand_8 (nand_8_out, AI[7], BI[7]);
  nand nand_9 (nand_9_out, AI[8], BI[8]);
  nand nand_10 (nand_10_out, AI[9], BI[9]);
  nand nand_11 (nand_11_out, AI[10], BI[10]);
  nand nand_12 (nand_12_out, AI[11], BI[11]);
  nand nand_13 (nand_13_out, AI[12], BI[12]);
  nand nand_14 (nand_14_out, AI[13], BI[13]);
  nand nand_15 (nand_15_out, AI[14], BI[14]);
  nand nand_16 (nand_16_out, AI[15], BI[15]);
  nand nand_17 (nand_17_out, nand_1_out, nand_1_out);
  nand nand_18 (nand_18_out, nand_2_out, nand_2_out);
  nand nand_19 (nand_19_out, nand_3_out, nand_3_out);
  nand nand_20 (nand_20_out, nand_4_out, nand_4_out);
  nand nand_21 (nand_21_out, nand_5_out, nand_5_out);
  nand nand_22 (nand_22_out, nand_6_out, nand_6_out);
  nand nand_23 (nand_23_out, nand_7_out, nand_7_out);
  nand nand_24 (nand_24_out, nand_8_out, nand_8_out);
  nand nand_25 (nand_25_out, nand_9_out, nand_9_out);
  nand nand_26 (nand_26_out, nand_10_out, nand_10_out);
  nand nand_27 (nand_27_out, nand_11_out, nand_11_out);
  nand nand_28 (nand_28_out, nand_12_out, nand_12_out);
  nand nand_29 (nand_29_out, nand_13_out, nand_13_out);
  nand nand_30 (nand_30_out, nand_14_out, nand_14_out);
  nand nand_31 (nand_31_out, nand_15_out, nand_15_out);
  nand nand_32 (nand_32_out, nand_16_out, nand_16_out);
  or or_1 (OUT, nand_17_out, nand_18_out, nand_19_out, nand_20_out, nand_21_out, nand_22_out, nand_23_out, nand_24_out, nand_25_out, nand_26_out, nand_27_out, nand_28_out, nand_29_out, nand_30_out, nand_31_out, nand_32_out);
  // Pins of 8 and 16 bits meet at BI
  // Pins of 9 and 16 bits meet at AI

  // Notes on the sheet:
  //   Schottky diode 
  //   OR
endmodule
