// Digital circuit oprom.dig as structural Verilog
module oprom (
  input  [3:0] OPCODE,
  output REGWEN,
  output ADRWEN,
  output IOREN,
  output IOWEN,
  output PCSSEL,
  output HALT
);

  wire nand_1_out, nand_2_out, nand_3_out, nand_4_out, nand_5_out;
  wire [7:5] rom_1_d;

  nand nand_1 (nand_1_out, OPCODE[3], OPCODE[2]);
  nand nand_2 (nand_2_out, OPCODE[1], OPCODE[0]);
  nand nand_3 (nand_3_out, nand_1_out, nand_1_out);
  nand nand_4 (nand_4_out, nand_2_out, nand_2_out);
  ROM #(.AddrBits(4), .Bits(8)) rom_1 (.A(OPCODE), .sel(1'b1), .D({rom_1_d, PCSSEL, IOWEN, IOREN, ADRWEN, REGWEN}));
  nand nand_5 (nand_5_out, nand_3_out, nand_4_out);
  nand nand_6 (HALT, nand_5_out, nand_5_out);

  // Notes on the sheet:
  //   rom_1 loads microcode.bin
endmodule
