// Digital circuit out_register.dig as structural Verilog
module out_register (
  input  [7:0] DATA,
  input  WEN,
  output [7:0] OUT
);

  wire nand_1_out, nand_2_out, nand_3_out, nand_4_out, nand_5_out, nand_6_out, nand_7_out, nand_8_out,
       nand_9_out, nand_10_out, nand_11_out, nand_12_out, nand_13_out, nand_14_out, nand_15_out, nand_16_out,
       nand_17_out, nand_18_out, nand_19_out, nand_20_out, nand_21_out, nand_22_out, nand_23_out,
       nand_24_out, nand_26_out, nand_28_out, nand_30_out, nand_32_out, nand_34_out, nand_36_out,
       nand_38_out, nand_40_out;

  nand nand_1 (nand_1_out, DATA[0], DATA[0]);
  nand nand_2 (nand_2_out, DATA[1], DATA[1]);
  nand nand_3 (nand_3_out, DATA[2], DATA[2]);
  nand nand_4 (nand_4_out, DATA[3], DATA[3]);
  nand nand_5 (nand_5_out, DATA[4], DATA[4]);
  nand nand_6 (nand_6_out, DATA[5], DATA[5]);
  nand nand_7 (nand_7_out, DATA[6], DATA[6]);
  nand nand_8 (nand_8_out, DATA[7], DATA[7]);
  nand nand_9 (nand_9_out, DATA[0], WEN);
  nand nand_10 (nand_10_out, WEN, nand_1_out);
  nand nand_11 (nand_11_out, DATA[1], WEN);
  nand nand_12 (nand_12_out, WEN, nand_2_out);
  nand nand_13 (nand_13_out, DATA[2], WEN);
  nand nand_14 (nand_14_out, WEN, nand_3_out);
  nand nand_15 (nand_15_out, DATA[3], WEN);
  nand nand_16 (nand_16_out, WEN, nand_4_out);
  nand nand_17 (nand_17_out, DATA[4], WEN);
  nand nand_18 (nand_18_out, WEN, nand_5_out);
  nand nand_19 (nand_19_out, DATA[5], WEN);
  nand nand_20 (nand_20_out, WEN, nand_6_out);
  nand nand_21 (nand_21_out, DATA[6], WEN);
  nand nand_22 (nand_22_out, WEN, nand_7_out);
  nand nand_23 (nand_23_out, DATA[7], WEN);
  nand nand_24 (nand_24_out, WEN, nand_8_out);
  nand nand_25 (OUT[0], nand_9_out, nand_26_out);
  nand nand_26 (nand_26_out, OUT[0], nand_10_out);
  nand nand_27 (OUT[1], nand_11_out, nand_28_out);
  nand nand_28 (nand_28_out, OUT[1], nand_12_out);
  nand nand_29 (OUT[2], nand_13_out, nand_30_out);
  nand nand_30 (nand_30_out, OUT[2], nand_14_out);
  nand nand_31 (OUT[3], nand_15_out, nand_32_out);
  nand nand_32 (nand_32_out, OUT[3], nand_16_out);
  nand nand_33 (OUT[4], nand_17_out, nand_34_out);
  nand nand_34 (nand_34_out, OUT[4], nand_18_out);
  nand nand_35 (OUT[5], nand_19_out, nand_36_out);
  nand nand_36 (nand_36_out, OUT[5], nand_20_out);
  nand nand_37 (OUT[6], nand_21_out, nand_38_out);
  nand nand_38 (nand_38_out, OUT[6], nand_22_out);
  nand nand_39 (OUT[7], nand_23_out, nand_40_out);
  nand nand_40 (nand_40_out, OUT[7], nand_24_out);
endmodule
