// Digital circuit program_counter.dig as structural Verilog
module program_counter (
  input  CLK,
  input  [15:0] W,
  input  CLR,
  output [15:0] R
);

  _8bit_register_async_clear _8bit_register_async_clear_1 (
    .CLK(CLK), .WEN(1'b1), .WRITE(W[7:0]), .CLR(CLR), .READ(R[7:0]));
  _8bit_register_async_clear _8bit_register_async_clear_2 (
    .CLK(CLK), .WEN(1'b1), .WRITE(W[15:8]), .CLR(CLR), .READ(R[15:8]));
endmodule
