// Digital circuit register_bank.dig as structural Verilog
module register_bank (
  input  CLK,
  input  CLR,
  input  [2:0] WSEL,
  input  [2:0] RSEL0,
  input  [2:0] RSEL1,
  input  [7:0] DATA_GP,
  input  [7:0] DATA_FLAG,
  input  [15:0] DATA_ADDR,
  input  WRITE_GP,
  input  WRITE_FLAG,
  input  WRITE_ADDR,
  output [7:0] READ_0,
  output [7:0] READ_1,
  output [7:0] READ_FLAG,
  output [15:0] READ_ADDR
);

  wire nand_1_out, nand_2_out, nand_3_out, nand_4_out, nand_5_out, nand_6_out, nand_7_out, nand_8_out,
       nand_9_out, nand_10_out, nand_11_out, nand_12_out, nand_13_out, nand_14_out, nand_15_out, nand_16_out,
       nand_17_out;
  wire [7:0] _2x8bit_mux_1_out, _2x8bit_mux_2_out, _2x8bit_mux_3_out, _3bit_decode_1_out,
       _8bit_register_async_clear_1_read, _8bit_register_async_clear_2_read,
       _8bit_register_async_clear_3_read, _8bit_register_async_clear_4_read, _8x8bit_interleave_1_out0,
       _8x8bit_interleave_1_out1, _8x8bit_interleave_1_out2, _8x8bit_interleave_1_out3,
       _8x8bit_interleave_1_out4, _8x8bit_interleave_1_out5, _8x8bit_interleave_1_out6,
       _8x8bit_interleave_1_out7;

  _3bit_decode _3bit_decode_1 (.IN(WSEL), .OUT(_3bit_decode_1_out));
  nand nand_1 (nand_1_out, _3bit_decode_1_out[1], WRITE_GP);
  nand nand_2 (nand_2_out, _3bit_decode_1_out[2], WRITE_GP);
  nand nand_3 (nand_3_out, _3bit_decode_1_out[3], WRITE_GP);
  nand nand_4 (nand_4_out, _3bit_decode_1_out[4], WRITE_GP);
  nand nand_5 (nand_5_out, _3bit_decode_1_out[5], WRITE_GP);
  nand nand_6 (nand_6_out, WRITE_FLAG, WRITE_FLAG);
  nand nand_7 (nand_7_out, _3bit_decode_1_out[6], WRITE_GP);
  nand nand_8 (nand_8_out, WRITE_ADDR, WRITE_ADDR);
  nand nand_9 (nand_9_out, _3bit_decode_1_out[7], WRITE_GP);
  nand nand_10 (nand_10_out, WRITE_ADDR, WRITE_ADDR);
  nand nand_11 (nand_11_out, nand_1_out, nand_1_out);
  nand nand_12 (nand_12_out, nand_2_out, nand_2_out);
  nand nand_13 (nand_13_out, nand_3_out, nand_3_out);
  nand nand_14 (nand_14_out, nand_4_out, nand_4_out);
  nand nand_15 (nand_15_out, nand_5_out, nand_6_out);
  nand nand_16 (nand_16_out, nand_7_out, nand_8_out);
  nand nand_17 (nand_17_out, nand_9_out, nand_10_out);
  _2x8bit_mux _2x8bit_mux_1 (.SEL(WRITE_FLAG), .B(DATA_FLAG), .A(DATA_GP), .OUT(_2x8bit_mux_1_out));
  _2x8bit_mux _2x8bit_mux_2 (.SEL(WRITE_ADDR), .B(DATA_ADDR[7:0]), .A(DATA_GP), .OUT(_2x8bit_mux_2_out));
  _2x8bit_mux _2x8bit_mux_3 (.SEL(WRITE_ADDR), .B(DATA_ADDR[15:8]), .A(DATA_GP), .OUT(_2x8bit_mux_3_out));
  _8bit_register_async_clear _8bit_register_async_clear_1 (
    .CLK(CLK), .WEN(nand_11_out), .WRITE(DATA_GP), .CLR(CLR), .READ(_8bit_register_async_clear_1_read));
  _8bit_register_async_clear _8bit_register_async_clear_2 (
    .CLK(CLK), .WEN(nand_12_out), .WRITE(DATA_GP), .CLR(CLR), .READ(_8bit_register_async_clear_2_read));
  _8bit_register_async_clear _8bit_register_async_clear_3 (
    .CLK(CLK), .WEN(nand_13_out), .WRITE(DATA_GP), .CLR(CLR), .READ(_8bit_register_async_clear_3_read));
  _8bit_register_async_clear _8bit_register_async_clear_4 (
    .CLK(CLK), .WEN(nand_14_out), .WRITE(DATA_GP), .CLR(CLR), .READ(_8bit_register_async_clear_4_read));
  _8bit_register_async_clear _8bit_register_async_clear_5 (
    .CLK(CLK), .WEN(nand_15_out), .WRITE(_2x8bit_mux_1_out), .CLR(CLR), .READ(READ_FLAG));
  _8bit_register_async_clear _8bit_register_async_clear_6 (
    .CLK(CLK), .WEN(nand_16_out), .WRITE(_2x8bit_mux_2_out), .CLR(CLR), .READ(READ_ADDR[7:0]));
  _8bit_register_async_clear _8bit_register_async_clear_7 (
    .CLK(CLK), .WEN(nand_17_out), .WRITE(_2x8bit_mux_3_out), .CLR(CLR), .READ(READ_ADDR[15:8]));
  _8x8bit_interleave _8x8bit_interleave_1 (
    .WORD0({8{1'b0}}), .WORD1(_8bit_register_async_clear_1_read), .WORD2(_8bit_register_async_clear_2_read),
    .WORD3(_8bit_register_async_clear_3_read), .WORD4(_8bit_register_async_clear_4_read), .WORD5(READ_FLAG),
    .WORD6(READ_ADDR[7:0]), .WORD7(READ_ADDR[15:8]), .OUT0(_8x8bit_interleave_1_out0),
    .OUT1(_8x8bit_interleave_1_out1), .OUT2(_8x8bit_interleave_1_out2), .OUT3(_8x8bit_interleave_1_out3),
    .OUT4(_8x8bit_interleave_1_out4), .OUT5(_8x8bit_interleave_1_out5), .OUT6(_8x8bit_interleave_1_out6),
    .OUT7(_8x8bit_interleave_1_out7));
  _8x8bit_masked_or _8x8bit_masked_or_1 (
    .SELECT(RSEL0), .DATA0(_8x8bit_interleave_1_out0), .DATA1(_8x8bit_interleave_1_out1),
    .DATA2(_8x8bit_interleave_1_out2), .DATA3(_8x8bit_interleave_1_out3), .DATA4(_8x8bit_interleave_1_out4),
    .DATA5(_8x8bit_interleave_1_out5), .DATA6(_8x8bit_interleave_1_out6), .DATA7(_8x8bit_interleave_1_out7),
    .OUT0(READ_0[0]), .OUT1(READ_0[1]), .OUT2(READ_0[2]), .OUT3(READ_0[3]), .OUT4(READ_0[4]),
    .OUT5(READ_0[5]), .OUT6(READ_0[6]), .OUT7(READ_0[7]));
  _8x8bit_masked_or _8x8bit_masked_or_2 (
    .SELECT(RSEL1), .DATA0(_8x8bit_interleave_1_out0), .DATA1(_8x8bit_interleave_1_out1),
    .DATA2(_8x8bit_interleave_1_out2), .DATA3(_8x8bit_interleave_1_out3), .DATA4(_8x8bit_interleave_1_out4),
    .DATA5(_8x8bit_interleave_1_out5), .DATA6(_8x8bit_interleave_1_out6), .DATA7(_8x8bit_interleave_1_out7),
    .OUT0(READ_1[0]), .OUT1(READ_1[1]), .OUT2(READ_1[2]), .OUT3(READ_1[3]), .OUT4(READ_1[4]),
    .OUT5(READ_1[5]), .OUT6(READ_1[6]), .OUT7(READ_1[7]));

  // Notes on the sheet:
  //   NULL register
endmodule
