// Digital circuit select2.dig as structural Verilog
module select2 (
  input  S0,
  input  S1,
  output O0,
  output O1,
  output O2,
  output O3
);

  wire nand_1_out, nand_2_out, nand_3_out, nand_4_out, nand_5_out, nand_6_out;

  nand nand_1 (nand_1_out, S0, S0);
  nand nand_2 (nand_2_out, S1, S1);
  nand nand_3 (nand_3_out, nand_1_out, nand_2_out);
  nand nand_4 (nand_4_out, S0, nand_2_out);
  nand nand_5 (nand_5_out, nand_1_out, S1);
  nand nand_6 (nand_6_out, S0, S1);
  nand nand_7 (O0, nand_3_out, nand_3_out);
  nand nand_8 (O1, nand_4_out, nand_4_out);
  nand nand_9 (O2, nand_5_out, nand_5_out);
  nand nand_10 (O3, nand_6_out, nand_6_out);
endmodule
